// Logisim project CPU.circ as structural Verilog: 9 circuits, main circuit main
module main (
);

  wire and_1_out, and_2_out, Clock_out, controller_1_acc_cache_write, controller_1_acc_dest,
       controller_1_acc_source, controller_1_acc_write, controller_1_acc_write_on_bus,
       controller_1_arithm_add, controller_1_arithm_div, controller_1_arithm_mul, controller_1_arithm_sub,
       controller_1_instruction_dest, controller_1_instruction_write_on_bus, controller_1_ram_dest,
       controller_1_ram_source, controller_1_ram_write, controller_1_ram_write_on_bus, controller_1_reset_tc,
       counter_1_tick_0, counter_1_tick_1, counter_1_tick_2, counter_1_tick_3, counter_1_tick_4;
  wire [7:0] controlled_buffer_1_out, controlled_buffer_2_out, IP_cache_q, IP_q, rom_1_data;
  wire [15:8] rom_1_data_2;

  Counter counter_1 (
    .CLOCK(Clock_out), .RESET(controller_1_reset_tc), .TICK_0(counter_1_tick_0), .TICK_1(counter_1_tick_1),
    .TICK_2(counter_1_tick_2), .TICK_3(counter_1_tick_3), .TICK_4(counter_1_tick_4));
  Clock Clock (.out(Clock_out));
  Counter_part IP (.Q(IP_q), .clk(counter_1_tick_0));  // open: load, D, count, carry, clr
  Controller controller_1 (
    .INSTRUCTION(rom_1_data), .TICK0(counter_1_tick_0), .TICK1(counter_1_tick_1), .TICK2(counter_1_tick_2),
    .TICK3(counter_1_tick_3), .TICK4(counter_1_tick_4), .RESET_TC(controller_1_reset_tc),
    .RAM_WRITE(controller_1_ram_write), .RAM_DEST(controller_1_ram_dest),
    .RAM_SOURCE(controller_1_ram_source), .RAM_WRITE_ON_BUS(controller_1_ram_write_on_bus),
    .ACC_DEST(controller_1_acc_dest), .ACC_SOURCE(controller_1_acc_source),
    .ACC_WRITE_ON_BUS(controller_1_acc_write_on_bus), .ACC_WRITE(controller_1_acc_write),
    .ACC_CACHE_WRITE(controller_1_acc_cache_write), .INSTRUCTION_DEST(controller_1_instruction_dest),
    .INSTRUCTION_WRITE_ON_BUS(controller_1_instruction_write_on_bus), .ARITHM_ADD(controller_1_arithm_add),
    .ARITHM_SUB(controller_1_arithm_sub), .ARITHM_MUL(controller_1_arithm_mul),
    .ARITHM_DIV(controller_1_arithm_div));
  Register IP_cache (.D(IP_q), .Q(IP_cache_q), .clk(counter_1_tick_0));  // open: en, clr
  ROM_part #(.dataWidth(16)) rom_1 (.addr(IP_cache_q), .data({rom_1_data_2, rom_1_data}), .sel(1'b1));
  and and_1 (and_1_out, ~controller_1_instruction_dest, controller_1_instruction_write_on_bus);  // AND_Gate
  and and_2 (and_2_out, controller_1_instruction_dest, controller_1_instruction_write_on_bus);
  assign controlled_buffer_1_out = and_1_out ? rom_1_data_2 : 8'bz;  // Controlled_Buffer controlled_buffer_1
  assign controlled_buffer_2_out = and_2_out ? rom_1_data_2 : 8'bz;  // Controlled_Buffer controlled_buffer_2
  Pull_Resistor pull_resistor_1 (.node(controlled_buffer_2_out));
  Pull_Resistor pull_resistor_2 (.node(controlled_buffer_1_out));
  RAM ram_1 (
    .ADDRESS(controlled_buffer_2_out), .DATA(controlled_buffer_1_out), .WRITE(controller_1_ram_write),
    .CLOCK(Clock_out), .DESTINATION(controller_1_ram_dest), .SOURCE(controller_1_ram_source),
    .WRITE_ON_BUS(controller_1_ram_write_on_bus), .DATA_2(controlled_buffer_1_out),
    .ADDRESS_2(controlled_buffer_2_out));  // open: WRITE_CACHE
  ALU alu_1 (
    .DATA(controlled_buffer_1_out), .CACHE_WRITE(controller_1_acc_cache_write),
    .WRITE(controller_1_acc_write), .CLOCK(Clock_out), .ARITHM_SELECT_ADD(controller_1_arithm_add),
    .ARITHM_SELECT_SUB(controller_1_arithm_sub), .ARITHM_SELECT_MUL(controller_1_arithm_mul),
    .ARITHM_SELECT_DIV(controller_1_arithm_div), .DESTINATION(controller_1_acc_dest),
    .SOURCE(controller_1_acc_source), .WRITE_ON_BUS(controller_1_acc_write_on_bus),
    .DATA_2(controlled_buffer_1_out), .ADDRESS(controlled_buffer_2_out));

  // Notes on the sheet:
  //   contents of rom_1 (hex, n*v repeats v):
  //   3402 3 2b02 103 1 203 508 303
  //   DATA_BUS
  //   ADDRESS_BUS
endmodule

// AccLoad
module _0x01_02_AccLoad (
  input  TICK_1,
  input  [7:0] INSTRUCTION,
  output RESET_TC,
  output ACC_WRITE,
  output INSTRUCTION_WRITE_ON_BUS,
  output RAM_WRITE_ON_BUS,
  output INSTRUCTION_DEST
);

  wire comparator_2_eq;

  Comparator comparator_1 (.a(INSTRUCTION), .b(8'h1), .eq(INSTRUCTION_DEST));  // open: gt, lt
  Comparator comparator_2 (.a(INSTRUCTION), .b(8'h2), .eq(comparator_2_eq));  // open: gt, lt
  or or_1 (ACC_WRITE, INSTRUCTION_DEST, comparator_2_eq);
  and and_1 (RESET_TC, TICK_1, ACC_WRITE);

  assign INSTRUCTION_WRITE_ON_BUS = ACC_WRITE;
  assign RAM_WRITE_ON_BUS = INSTRUCTION_DEST;
endmodule

module ALU (
  input  [7:0] DATA,
  input  CACHE_WRITE,
  input  WRITE,
  input  CLOCK,
  input  ARITHM_SELECT_ADD,
  input  ARITHM_SELECT_SUB,
  input  ARITHM_SELECT_MUL,
  input  ARITHM_SELECT_DIV,
  input  DESTINATION,
  input  SOURCE,
  input  WRITE_ON_BUS,
  output [7:0] DATA_2,
  output [7:0] ADDRESS
);

  wire and_1_out, and_2_out, and_3_out, and_4_out, and_5_out, and_6_out, or_1_out;
  wire [7:0] Accumulator_q, adder_1_out, controlled_buffer_1_out, divider_1_out, multiplexer_1_out,
       multiplier_1_out, register_1_q, subtractor_1_out;

  Multiplexer #(.width(8)) multiplexer_1 (
    .in0(DATA), .in1(controlled_buffer_1_out), .out(multiplexer_1_out), .sel(or_1_out));  // open: en
  or or_1 (or_1_out, ARITHM_SELECT_ADD, ARITHM_SELECT_SUB, ARITHM_SELECT_MUL, ARITHM_SELECT_DIV);
  and and_1 (and_1_out, WRITE, CLOCK);
  Register Accumulator (.D(multiplexer_1_out), .en(1'b1), .Q(Accumulator_q), .clk(and_1_out));  // open: clr
  and and_2 (and_2_out, CACHE_WRITE, CLOCK);
  Register register_1 (.D(Accumulator_q), .en(1'b1), .Q(register_1_q), .clk(and_2_out));  // open: clr
  assign controlled_buffer_1_out = ARITHM_SELECT_ADD ? adder_1_out : 8'bz;  // Controlled_Buffer controlled_buffer_1
  assign controlled_buffer_1_out = ARITHM_SELECT_SUB ? subtractor_1_out : 8'bz;  // Controlled_Buffer controlled_buffer_2
  assign controlled_buffer_1_out = ARITHM_SELECT_MUL ? multiplier_1_out : 8'bz;  // Controlled_Buffer controlled_buffer_3
  assign controlled_buffer_1_out = ARITHM_SELECT_DIV ? divider_1_out : 8'bz;  // Controlled_Buffer controlled_buffer_4
  Adder adder_1 (.a(register_1_q), .b(DATA), .out(adder_1_out));  // open: cin, cout
  Subtractor subtractor_1 (.a(register_1_q), .b(DATA), .out(subtractor_1_out));  // open: bin, bout
  Multiplier multiplier_1 (.a(register_1_q), .b(DATA), .out(multiplier_1_out));  // open: cin, cout
  Divider divider_1 (.a(register_1_q), .b(DATA), .out(divider_1_out));  // open: upper, rem
  Comparator comparator_1 ();  // open: a, b, gt, eq, lt
  assign ADDRESS = and_3_out ? Accumulator_q : 8'bz;  // Controlled_Buffer controlled_buffer_5
  and and_3 (and_3_out, DESTINATION, ~SOURCE, WRITE_ON_BUS);  // AND_Gate
  assign ADDRESS = and_4_out ? register_1_q : 8'bz;  // Controlled_Buffer controlled_buffer_6
  assign DATA_2 = and_5_out ? Accumulator_q : 8'bz;  // Controlled_Buffer controlled_buffer_7
  and and_4 (and_4_out, DESTINATION, SOURCE, WRITE_ON_BUS);
  and and_5 (and_5_out, ~DESTINATION, ~SOURCE, WRITE_ON_BUS);  // AND_Gate
  assign DATA_2 = and_6_out ? register_1_q : 8'bz;  // Controlled_Buffer controlled_buffer_8
  and and_6 (and_6_out, ~DESTINATION, SOURCE, WRITE_ON_BUS);  // AND_Gate

  // Notes on the sheet:
  //   (0 -> DATA, 1 -> ADDRESS)
  //   (0 -> ACC, 1 -> CACHE)
endmodule

module RAM (
  input  [7:0] ADDRESS,
  input  [7:0] DATA,
  input  WRITE,
  input  CLOCK,
  input  WRITE_CACHE,
  input  DESTINATION,
  input  SOURCE,
  input  WRITE_ON_BUS,
  output [7:0] DATA_2,
  output [7:0] ADDRESS_2
);

  wire and_1_out, and_2_out, and_3_out, and_4_out, and_5_out;
  wire [7:0] ram_1_data, register_1_q;

  RAM_part #(.bus("separate")) ram_1 (
    .addr(ADDRESS), .din(DATA), .data(ram_1_data), .str(WRITE), .sel(1'b1), .clk(CLOCK), .ld(1'b1));  // open: clr
  and and_1 (and_1_out, CLOCK, WRITE_CACHE);
  Register register_1 (.D(ram_1_data), .en(1'b1), .Q(register_1_q), .clk(and_1_out));  // open: clr
  assign DATA_2 = and_2_out ? ram_1_data : 8'bz;  // Controlled_Buffer controlled_buffer_1
  assign ADDRESS_2 = and_3_out ? ram_1_data : 8'bz;  // Controlled_Buffer controlled_buffer_2
  and and_2 (and_2_out, ~DESTINATION, ~SOURCE, WRITE_ON_BUS);  // AND_Gate
  and and_3 (and_3_out, DESTINATION, ~SOURCE, WRITE_ON_BUS);  // AND_Gate
  assign ADDRESS_2 = and_5_out ? register_1_q : 8'bz;  // Controlled_Buffer controlled_buffer_3
  and and_4 (and_4_out, ~DESTINATION, SOURCE, WRITE_ON_BUS);  // AND_Gate
  and and_5 (and_5_out, DESTINATION, SOURCE, WRITE_ON_BUS);
  assign DATA_2 = and_4_out ? register_1_q : 8'bz;  // Controlled_Buffer controlled_buffer_4

  // Notes on the sheet:
  //   (0 -> DATA, 1 -> ADDRESS)
  //   (0 -> RAM, 1 -> CACHE)
endmodule

// AccSave
module _0x03_AccSave (
  input  TICK_1,
  input  [7:0] INSTRUCTION,
  output RESET_TC,
  output RAM_WRITE,
  output INSTRUCTION_DEST,
  output INSTRUCTION_WRITE_ON_BUS,
  output ACC_WRITE_ON_BUS
);

  Comparator comparator_1 (.a(INSTRUCTION), .b(8'h3), .eq(ACC_WRITE_ON_BUS));  // open: gt, lt
  and and_1 (RESET_TC, TICK_1, ACC_WRITE_ON_BUS);

  assign INSTRUCTION_DEST = ACC_WRITE_ON_BUS;
  assign INSTRUCTION_WRITE_ON_BUS = ACC_WRITE_ON_BUS;
  assign RAM_WRITE = ACC_WRITE_ON_BUS;
endmodule

module Counter (
  input  CLOCK,
  input  RESET,
  output TICK_0,
  output TICK_1,
  output TICK_2,
  output TICK_3,
  output TICK_4
);

  wire and_1_out, and_2_out, and_3_out, and_4_out, not_1_out, not_2_out, or_1_out, or_2_out;

  or or_1 (or_1_out, TICK_0, TICK_1, TICK_2, TICK_3, TICK_4);
  not not_1 (not_1_out, or_1_out);
  or or_2 (or_2_out, TICK_4, not_1_out, RESET);
  not not_2 (not_2_out, RESET);
  D_Flip_Flop d_ff_1 (.clk(CLOCK), .D(or_2_out), .Q(TICK_0), .en(1'b1));  // open: Qn, preset, reset
  and and_1 (and_1_out, TICK_0, not_2_out);
  D_Flip_Flop d_ff_2 (.clk(CLOCK), .D(and_1_out), .Q(TICK_1), .en(1'b1));  // open: Qn, preset, reset
  D_Flip_Flop d_ff_3 (.clk(CLOCK), .D(and_2_out), .Q(TICK_2), .en(1'b1));  // open: Qn, preset, reset
  and and_2 (and_2_out, TICK_1, not_2_out);
  and and_3 (and_3_out, TICK_2, not_2_out);
  D_Flip_Flop d_ff_4 (.clk(CLOCK), .D(and_3_out), .Q(TICK_3), .en(1'b1));  // open: Qn, preset, reset
  and and_4 (and_4_out, TICK_3, not_2_out);
  D_Flip_Flop d_ff_5 (.clk(CLOCK), .D(and_4_out), .Q(TICK_4), .en(1'b1));  // open: Qn, preset, reset
endmodule

module ROM (
);

  wire undriven;
  wire [7:0] IP_cache_q, IP_q;
  wire [15:0] rom_1_data;

  Counter_part IP (.Q(IP_q), .clk(undriven));  // open: load, D, count, carry, clr
  Register IP_cache (.D(IP_q), .Q(IP_cache_q), .clk(undriven));  // open: en, clr
  ROM_part #(.dataWidth(16)) rom_1 (.addr(IP_cache_q), .data(rom_1_data), .sel(1'b1));

  // Notes on the sheet:
  //   contents of rom_1 (hex, n*v repeats v):
  //   3402 3 2b02 103 1 203
endmodule

// CONTROLLER
module Controller (
  input  [7:0] INSTRUCTION,
  input  TICK0,
  input  TICK1,
  input  TICK2,
  input  TICK3,
  input  TICK4,
  output RESET_TC,
  output RAM_WRITE,
  output RAM_DEST,
  output RAM_SOURCE,
  output RAM_WRITE_ON_BUS,
  output ACC_DEST,
  output ACC_SOURCE,
  output ACC_WRITE_ON_BUS,
  output ACC_WRITE,
  output ACC_CACHE_WRITE,
  output INSTRUCTION_DEST,
  output INSTRUCTION_WRITE_ON_BUS,
  output ARITHM_ADD,
  output ARITHM_SUB,
  output ARITHM_MUL,
  output ARITHM_DIV
);

  wire n0x01_02_accload_1_acc_write, n0x01_02_accload_1_instruction_dest,
       n0x01_02_accload_1_instruction_write_on_bus, n0x01_02_accload_1_ram_write_on_bus,
       n0x01_02_accload_1_reset_tc, n0x03_accsave_1_acc_write_on_bus, n0x03_accsave_1_instruction_dest,
       n0x03_accsave_1_instruction_write_on_bus, n0x03_accsave_1_ram_write, n0x03_accsave_1_reset_tc,
       n0x04_05_06_07_08_09_0a_0b_arithmetic_1_acc_cache_write,
       n0x04_05_06_07_08_09_0a_0b_arithmetic_1_acc_write, n0x04_05_06_07_08_09_0a_0b_arithmetic_1_arithm_add,
       n0x04_05_06_07_08_09_0a_0b_arithmetic_1_arithm_div,
       n0x04_05_06_07_08_09_0a_0b_arithmetic_1_arithm_mul,
       n0x04_05_06_07_08_09_0a_0b_arithmetic_1_arithm_sub,
       n0x04_05_06_07_08_09_0a_0b_arithmetic_1_instruction_dest,
       n0x04_05_06_07_08_09_0a_0b_arithmetic_1_instruction_write_on_bus,
       n0x04_05_06_07_08_09_0a_0b_arithmetic_1_ram_write_on_bus,
       n0x04_05_06_07_08_09_0a_0b_arithmetic_1_reset_tc;

  _0x01_02_AccLoad u_0x01_02_accload_1 (
    .TICK_1(TICK1), .INSTRUCTION(INSTRUCTION), .RESET_TC(n0x01_02_accload_1_reset_tc),
    .ACC_WRITE(n0x01_02_accload_1_acc_write),
    .INSTRUCTION_WRITE_ON_BUS(n0x01_02_accload_1_instruction_write_on_bus),
    .RAM_WRITE_ON_BUS(n0x01_02_accload_1_ram_write_on_bus),
    .INSTRUCTION_DEST(n0x01_02_accload_1_instruction_dest));
  _0x03_AccSave u_0x03_accsave_1 (
    .TICK_1(TICK1), .INSTRUCTION(INSTRUCTION), .RESET_TC(n0x03_accsave_1_reset_tc),
    .RAM_WRITE(n0x03_accsave_1_ram_write), .INSTRUCTION_DEST(n0x03_accsave_1_instruction_dest),
    .INSTRUCTION_WRITE_ON_BUS(n0x03_accsave_1_instruction_write_on_bus),
    .ACC_WRITE_ON_BUS(n0x03_accsave_1_acc_write_on_bus));
  _0x04_05_06_07_08_09_0A_0B_Arithmetic u_0x04_05_06_07_08_09_0a_0b_arithmetic_1 (
    .TICK_0(TICK0), .TICK_1(TICK1), .TICK_2(TICK2), .INSTRUCTION(INSTRUCTION),
    .ARITHM_ADD(n0x04_05_06_07_08_09_0a_0b_arithmetic_1_arithm_add),
    .ARITHM_SUB(n0x04_05_06_07_08_09_0a_0b_arithmetic_1_arithm_sub),
    .ARITHM_MUL(n0x04_05_06_07_08_09_0a_0b_arithmetic_1_arithm_mul),
    .ARITHM_DIV(n0x04_05_06_07_08_09_0a_0b_arithmetic_1_arithm_div),
    .ACC_CACHE_WRITE(n0x04_05_06_07_08_09_0a_0b_arithmetic_1_acc_cache_write),
    .ACC_WRITE(n0x04_05_06_07_08_09_0a_0b_arithmetic_1_acc_write),
    .RESET_TC(n0x04_05_06_07_08_09_0a_0b_arithmetic_1_reset_tc),
    .INSTRUCTION_WRITE_ON_BUS(n0x04_05_06_07_08_09_0a_0b_arithmetic_1_instruction_write_on_bus),
    .INSTRUCTION_DEST(n0x04_05_06_07_08_09_0a_0b_arithmetic_1_instruction_dest),
    .RAM_WRITE_ON_BUS(n0x04_05_06_07_08_09_0a_0b_arithmetic_1_ram_write_on_bus));
  or u_RESET_TC (RESET_TC, n0x01_02_accload_1_reset_tc, n0x03_accsave_1_reset_tc, n0x04_05_06_07_08_09_0a_0b_arithmetic_1_reset_tc);
  buf or_1 (RAM_WRITE, n0x03_accsave_1_ram_write);  // OR_Gate
  buf or_2 (RAM_DEST, 1'b0);  // OR_Gate
  buf or_3 (RAM_SOURCE, 1'b0);  // OR_Gate
  or or_4 (RAM_WRITE_ON_BUS, n0x01_02_accload_1_ram_write_on_bus, n0x04_05_06_07_08_09_0a_0b_arithmetic_1_ram_write_on_bus);
  buf or_5 (ACC_DEST, 1'b0);  // OR_Gate
  buf or_6 (ACC_SOURCE, 1'b0);  // OR_Gate
  buf or_7 (ACC_WRITE_ON_BUS, n0x03_accsave_1_acc_write_on_bus);  // OR_Gate
  or or_8 (ACC_WRITE, n0x01_02_accload_1_acc_write, n0x04_05_06_07_08_09_0a_0b_arithmetic_1_acc_write);
  buf or_9 (ACC_CACHE_WRITE, n0x04_05_06_07_08_09_0a_0b_arithmetic_1_acc_cache_write);  // OR_Gate
  or or_10 (INSTRUCTION_DEST, n0x01_02_accload_1_instruction_dest, n0x03_accsave_1_instruction_dest, n0x04_05_06_07_08_09_0a_0b_arithmetic_1_instruction_dest);
  or or_11 (INSTRUCTION_WRITE_ON_BUS, n0x01_02_accload_1_instruction_write_on_bus, n0x03_accsave_1_instruction_write_on_bus, n0x04_05_06_07_08_09_0a_0b_arithmetic_1_instruction_write_on_bus);
  buf or_12 (ARITHM_ADD, n0x04_05_06_07_08_09_0a_0b_arithmetic_1_arithm_add);  // OR_Gate
  buf or_13 (ARITHM_SUB, n0x04_05_06_07_08_09_0a_0b_arithmetic_1_arithm_sub);  // OR_Gate
  buf or_14 (ARITHM_MUL, n0x04_05_06_07_08_09_0a_0b_arithmetic_1_arithm_mul);  // OR_Gate
  buf or_15 (ARITHM_DIV, n0x04_05_06_07_08_09_0a_0b_arithmetic_1_arithm_div);  // OR_Gate

  // Notes on the sheet:
  //   (0 -> DATA, 1 -> ADDRESS)
endmodule

// Arithmetic
module _0x04_05_06_07_08_09_0A_0B_Arithmetic (
  input  TICK_0,
  input  TICK_1,
  input  TICK_2,
  input  [7:0] INSTRUCTION,
  output ARITHM_ADD,
  output ARITHM_SUB,
  output ARITHM_MUL,
  output ARITHM_DIV,
  output ACC_CACHE_WRITE,
  output ACC_WRITE,
  output RESET_TC,
  output INSTRUCTION_WRITE_ON_BUS,
  output INSTRUCTION_DEST,
  output RAM_WRITE_ON_BUS
);

  wire comparator_1_eq, comparator_2_eq, comparator_3_eq, comparator_4_eq, comparator_5_eq, comparator_6_eq,
       comparator_7_eq, comparator_8_eq;

  Comparator comparator_1 (.a(INSTRUCTION), .b(8'h4), .eq(comparator_1_eq));  // open: gt, lt
  Comparator comparator_2 (.a(INSTRUCTION), .b(8'h5), .eq(comparator_2_eq));  // open: gt, lt
  Comparator comparator_3 (.a(INSTRUCTION), .b(8'h6), .eq(comparator_3_eq));  // open: gt, lt
  Comparator comparator_4 (.a(INSTRUCTION), .b(8'h7), .eq(comparator_4_eq));  // open: gt, lt
  Comparator comparator_5 (.a(INSTRUCTION), .b(8'h8), .eq(comparator_5_eq));  // open: gt, lt
  Comparator comparator_6 (.a(INSTRUCTION), .b(8'h9), .eq(comparator_6_eq));  // open: gt, lt
  Comparator comparator_7 (.a(INSTRUCTION), .b(8'ha), .eq(comparator_7_eq));  // open: gt, lt
  Comparator comparator_8 (.a(INSTRUCTION), .b(8'hb), .eq(comparator_8_eq));  // open: gt, lt
  or or_1 (INSTRUCTION_DEST, comparator_4_eq, comparator_3_eq, comparator_2_eq, comparator_1_eq);
  or or_2 (ARITHM_ADD, comparator_1_eq, comparator_5_eq);
  or or_3 (ARITHM_SUB, comparator_2_eq, comparator_6_eq);
  or or_4 (ARITHM_MUL, comparator_3_eq, comparator_7_eq);
  or or_5 (ARITHM_DIV, comparator_4_eq, comparator_8_eq);
  or or_6 (INSTRUCTION_WRITE_ON_BUS, ARITHM_ADD, ARITHM_SUB, ARITHM_MUL, ARITHM_DIV);
  and and_1 (ACC_CACHE_WRITE, TICK_0, INSTRUCTION_WRITE_ON_BUS);
  and and_2 (ACC_WRITE, TICK_1, INSTRUCTION_WRITE_ON_BUS);
  and and_3 (RESET_TC, TICK_2, INSTRUCTION_WRITE_ON_BUS);

  assign RAM_WRITE_ON_BUS = INSTRUCTION_DEST;

  // Notes on the sheet:
  //   IMMEDIATE
endmodule
