// Logisim project CPU_2.circ as structural Verilog: 16 circuits, main circuit main
module main (
);

  wire alu_1_equals, alu_1_greater_than, alu_1_less_than, and_1_out, and_2_out, and_3_out, and_4_out,
       Clock_out, controller_1_acc_cache_write, controller_1_acc_dest, controller_1_acc_source,
       controller_1_acc_write, controller_1_acc_write_on_bus, controller_1_arithm_add,
       controller_1_arithm_div, controller_1_arithm_mul, controller_1_arithm_sub,
       controller_1_da_cache_write, controller_1_da_cache_write_on_bus, controller_1_instruction_dest,
       controller_1_instruction_write_on_bus, controller_1_ip_load, controller_1_ip_source,
       controller_1_logic_and, controller_1_logic_invert, controller_1_logic_or, controller_1_logic_xor,
       controller_1_reset_tc, counter_1_tick_0, counter_1_tick_1, counter_1_tick_2, counter_1_tick_3,
       counter_1_tick_4, or_1_out;
  wire [7:0] adder_1_out, alu_1_address, alu_1_data_2, controller_1_ctrl, DA_CACHE_q, IP_cache_q, IP_q,
       multiplexer_1_out, rom_1_data;
  wire [15:8] rom_1_data_2;

  Clock Clock (.out(Clock_out));
  Counter counter_1 (
    .CLOCK(Clock_out), .RESET(controller_1_reset_tc), .TICK_0(counter_1_tick_0), .TICK_1(counter_1_tick_1),
    .TICK_2(counter_1_tick_2), .TICK_3(counter_1_tick_3), .TICK_4(counter_1_tick_4));
  Controller controller_1 (
    .INSTRUCTION(rom_1_data), .CLOCK(Clock_out), .TICK0(counter_1_tick_0), .TICK1(counter_1_tick_1),
    .TICK2(counter_1_tick_2), .TICK3(counter_1_tick_3), .TICK4(counter_1_tick_4), .EQUALS(alu_1_equals),
    .GREATER_THAN(alu_1_greater_than), .LESS_THAN(alu_1_less_than), .RESET_TC(controller_1_reset_tc),
    .CTRL(controller_1_ctrl), .ACC_DEST(controller_1_acc_dest), .ACC_SOURCE(controller_1_acc_source),
    .ACC_WRITE_ON_BUS(controller_1_acc_write_on_bus), .ACC_WRITE(controller_1_acc_write),
    .ACC_CACHE_WRITE(controller_1_acc_cache_write), .INSTRUCTION_DEST(controller_1_instruction_dest),
    .INSTRUCTION_WRITE_ON_BUS(controller_1_instruction_write_on_bus), .ARITHM_ADD(controller_1_arithm_add),
    .ARITHM_SUB(controller_1_arithm_sub), .ARITHM_MUL(controller_1_arithm_mul),
    .ARITHM_DIV(controller_1_arithm_div), .LOGIC_AND(controller_1_logic_and),
    .LOGIC_OR(controller_1_logic_or), .LOGIC_XOR(controller_1_logic_xor),
    .LOGIC_INVERT(controller_1_logic_invert), .IP_LOAD(controller_1_ip_load),
    .IP_SOURCE(controller_1_ip_source), .DA_CACHE_WRITE(controller_1_da_cache_write),
    .DA_CACHE_WRITE_ON_BUS(controller_1_da_cache_write_on_bus));
  Multiplexer #(.width(8)) multiplexer_1 (
    .in0(adder_1_out), .in1(alu_1_data_2), .out(multiplexer_1_out), .sel(controller_1_ip_source));  // open: en
  Register IP (.D(multiplexer_1_out), .Q(IP_q), .clk(or_1_out));  // open: en, clr
  or or_1 (or_1_out, and_1_out, and_2_out);
  and and_1 (and_1_out, counter_1_tick_0, ~and_2_out);  // AND_Gate
  and and_2 (and_2_out, Clock_out, controller_1_ip_load);
  Adder adder_1 (.a(8'h1), .b(IP_q), .out(adder_1_out));  // open: cin, cout
  Register IP_cache (.D(IP_q), .en(1'b1), .Q(IP_cache_q), .clk(counter_1_tick_0));  // open: clr
  ALU alu_1 (
    .DATA(alu_1_data_2), .CACHE_WRITE(controller_1_acc_cache_write), .WRITE(controller_1_acc_write),
    .CLOCK(Clock_out), .ARITHM_SELECT_ADD(controller_1_arithm_add),
    .ARITHM_SELECT_SUB(controller_1_arithm_sub), .ARITHM_SELECT_MUL(controller_1_arithm_mul),
    .ARITHM_SELECT_DIV(controller_1_arithm_div), .LOGIC_SELECT_AND(controller_1_logic_and),
    .LOGIC_SELECT_OR(controller_1_logic_or), .LOGIC_SELECT_XOR(controller_1_logic_xor),
    .LOGIC_SELECT_INVERT(controller_1_logic_invert), .DESTINATION(controller_1_acc_dest),
    .SOURCE(controller_1_acc_source), .WRITE_ON_BUS(controller_1_acc_write_on_bus),
    .GREATER_THAN(alu_1_greater_than), .EQUALS(alu_1_equals), .LESS_THAN(alu_1_less_than),
    .DATA_2(alu_1_data_2), .ADDRESS(alu_1_address));
  ROM_part #(.dataWidth(16)) rom_1 (.addr(IP_cache_q), .data({rom_1_data_2, rom_1_data}));  // open: sel
  and and_3 (and_3_out, ~controller_1_instruction_dest, controller_1_instruction_write_on_bus);  // AND_Gate
  assign alu_1_data_2 = and_3_out ? rom_1_data_2 : 8'bz;  // Controlled_Buffer controlled_buffer_1
  and and_4 (and_4_out, controller_1_instruction_dest, controller_1_instruction_write_on_bus);
  Pull_Resistor pull_resistor_1 (.node(alu_1_data_2));
  assign alu_1_address = and_4_out ? rom_1_data_2 : 8'bz;  // Controlled_Buffer controlled_buffer_2
  Register DA_CACHE (.D(alu_1_data_2), .Q(DA_CACHE_q), .clk(controller_1_da_cache_write));  // open: en, clr
  assign alu_1_address = controller_1_da_cache_write_on_bus ? DA_CACHE_q : 8'bz;  // Controlled_Buffer controlled_buffer_3
  Pull_Resistor pull_resistor_2 (.node(alu_1_address));
  Pull_Resistor pull_resistor_3 (.node(controller_1_ctrl));
  RAM ram_1 (.ADDRESS(alu_1_address), .DATA(alu_1_data_2), .CONTROL(controller_1_ctrl), .DATA_2(alu_1_data_2));

  // Notes on the sheet:
  //   contents of rom_1 (hex, n*v repeats v):
  //   3481 83 2b81 183 1 283 584 383 301 184 383 3c0f 888 1081 83 3
  //   DATA_BUS
  //   ADDRESS_BUS
  //   Memory devices
  //   CONTROL_BUS
endmodule

// AccLoad
module _0x01_81_AccLoad (
  input  TICK_1,
  input  [7:0] INSTRUCTION,
  output RESET_TC,
  output ACC_WRITE,
  output INSTRUCTION_WRITE_ON_BUS,
  output RAM_WRITE_ON_BUS,
  output INSTRUCTION_DEST
);

  wire [6:0] bit_extender_1_out;

  Bit_Extender #(.out_width(7)) bit_extender_1 (.in(INSTRUCTION), .out(bit_extender_1_out));
  Comparator #(.width(7), .mode("unsigned")) comparator_1 (
    .a(bit_extender_1_out), .b(7'b0000001), .eq(ACC_WRITE));  // open: gt, lt
  and and_1 (RESET_TC, TICK_1, ACC_WRITE);
  and and_2 (INSTRUCTION_DEST, ~INSTRUCTION[7], ACC_WRITE);  // AND_Gate

  assign INSTRUCTION_WRITE_ON_BUS = ACC_WRITE;
  assign RAM_WRITE_ON_BUS = INSTRUCTION_DEST;
endmodule

module ALU (
  input  [7:0] DATA,
  input  CACHE_WRITE,
  input  WRITE,
  input  CLOCK,
  input  ARITHM_SELECT_ADD,
  input  ARITHM_SELECT_SUB,
  input  ARITHM_SELECT_MUL,
  input  ARITHM_SELECT_DIV,
  input  LOGIC_SELECT_AND,
  input  LOGIC_SELECT_OR,
  input  LOGIC_SELECT_XOR,
  input  LOGIC_SELECT_INVERT,
  input  DESTINATION,
  input  SOURCE,
  input  WRITE_ON_BUS,
  output GREATER_THAN,
  output EQUALS,
  output LESS_THAN,
  output [7:0] DATA_2,
  output [7:0] ADDRESS
);

  wire and_1_out, and_2_out, and_3_out, and_4_out, and_5_out, and_6_out, or_1_out, or_2_out;
  wire [7:0] Accumulator_q, adder_1_out, bitwise_and_1_out_3, bitwise_or_1_out_3, bitwise_xor_1_out_3,
       controlled_buffer_1_out, divider_1_out, multiplexer_1_out, multiplier_1_out, n8bit_inverter_1_out_2,
       register_1_q, subtractor_1_out;

  Multiplexer #(.width(8)) multiplexer_1 (
    .in0(DATA), .in1(controlled_buffer_1_out), .out(multiplexer_1_out), .sel(or_1_out));  // open: en
  or or_1 (or_1_out, ARITHM_SELECT_ADD, ARITHM_SELECT_SUB, or_2_out, ARITHM_SELECT_MUL, ARITHM_SELECT_DIV);
  or or_2 (or_2_out, LOGIC_SELECT_AND, LOGIC_SELECT_OR, LOGIC_SELECT_XOR, LOGIC_SELECT_INVERT);
  and and_1 (and_1_out, WRITE, CLOCK);
  Register Accumulator (.D(multiplexer_1_out), .en(1'b1), .Q(Accumulator_q), .clk(and_1_out));  // open: clr
  and and_2 (and_2_out, CACHE_WRITE, CLOCK);
  Register register_1 (.D(Accumulator_q), .en(1'b1), .Q(register_1_q), .clk(and_2_out));  // open: clr
  assign controlled_buffer_1_out = ARITHM_SELECT_ADD ? adder_1_out : 8'bz;  // Controlled_Buffer controlled_buffer_1
  assign controlled_buffer_1_out = ARITHM_SELECT_SUB ? subtractor_1_out : 8'bz;  // Controlled_Buffer controlled_buffer_2
  assign controlled_buffer_1_out = ARITHM_SELECT_MUL ? multiplier_1_out : 8'bz;  // Controlled_Buffer controlled_buffer_3
  assign controlled_buffer_1_out = ARITHM_SELECT_DIV ? divider_1_out : 8'bz;  // Controlled_Buffer controlled_buffer_4
  assign controlled_buffer_1_out = LOGIC_SELECT_AND ? bitwise_and_1_out_3 : 8'bz;  // Controlled_Buffer controlled_buffer_5
  assign controlled_buffer_1_out = LOGIC_SELECT_OR ? bitwise_or_1_out_3 : 8'bz;  // Controlled_Buffer controlled_buffer_6
  assign controlled_buffer_1_out = LOGIC_SELECT_XOR ? bitwise_xor_1_out_3 : 8'bz;  // Controlled_Buffer controlled_buffer_7
  assign controlled_buffer_1_out = LOGIC_SELECT_INVERT ? n8bit_inverter_1_out_2 : 8'bz;  // Controlled_Buffer controlled_buffer_8
  Adder adder_1 (.a(register_1_q), .b(DATA), .out(adder_1_out));  // open: cin, cout
  Subtractor subtractor_1 (.a(register_1_q), .b(DATA), .out(subtractor_1_out));  // open: bin, bout
  Multiplier multiplier_1 (.a(register_1_q), .b(DATA), .out(multiplier_1_out));  // open: cin, cout
  Divider divider_1 (.a(register_1_q), .b(DATA), .out(divider_1_out));  // open: upper, rem
  BITWISE_AND bitwise_and_1 (.in_1(register_1_q), .in_2(DATA), .out_3(bitwise_and_1_out_3));
  BITWISE_OR bitwise_or_1 (.in_1(register_1_q), .in_2(DATA), .out_3(bitwise_or_1_out_3));
  BITWISE_XOR bitwise_xor_1 (.in_1(register_1_q), .in_2(DATA), .out_3(bitwise_xor_1_out_3));
  _8BIT_INVERTER u_8bit_inverter_1 (.in_1(register_1_q), .out_2(n8bit_inverter_1_out_2));
  assign ADDRESS = and_3_out ? Accumulator_q : 8'bz;  // Controlled_Buffer controlled_buffer_9
  and and_3 (and_3_out, DESTINATION, ~SOURCE, WRITE_ON_BUS);  // AND_Gate
  assign ADDRESS = and_4_out ? register_1_q : 8'bz;  // Controlled_Buffer controlled_buffer_10
  assign DATA_2 = and_5_out ? Accumulator_q : 8'bz;  // Controlled_Buffer controlled_buffer_11
  and and_4 (and_4_out, DESTINATION, SOURCE, WRITE_ON_BUS);
  and and_5 (and_5_out, ~DESTINATION, ~SOURCE, WRITE_ON_BUS);  // AND_Gate
  Comparator comparator_1 (.a(Accumulator_q), .b(DATA), .gt(GREATER_THAN), .eq(EQUALS), .lt(LESS_THAN));
  assign DATA_2 = and_6_out ? register_1_q : 8'bz;  // Controlled_Buffer controlled_buffer_12
  and and_6 (and_6_out, ~DESTINATION, SOURCE, WRITE_ON_BUS);  // AND_Gate

  // Notes on the sheet:
  //   (0 -> DATA, 1 -> ADDRESS)
  //   (0 -> ACC, 1 -> CACHE)
endmodule

module RAM (
  input  [7:0] ADDRESS,
  input  [7:0] DATA,
  input  [7:0] CONTROL,
  output [7:0] DATA_2
);

  wire and_1_out, and_2_out, not_1_out;
  wire [6:0] bit_extender_1_out;
  wire [7:0] ram_1_data;

  not not_1 (not_1_out, ADDRESS[7]);
  Bit_Extender #(.out_width(7)) bit_extender_1 (.in(ADDRESS), .out(bit_extender_1_out));
  and and_1 (and_1_out, not_1_out, CONTROL[0]);
  RAM_part #(.addrWidth(7), .bus("separate")) ram_1 (
    .addr(bit_extender_1_out), .din(DATA), .data(ram_1_data), .str(and_1_out), .sel(1'b1), .clk(CONTROL[2]),
    .ld(1'b1));  // open: clr
  and and_2 (and_2_out, not_1_out, CONTROL[1]);
  assign DATA_2 = and_2_out ? ram_1_data : 8'bz;  // Controlled_Buffer controlled_buffer_1
endmodule

// AccWriteOnBus
module _0x03_83_AccWriteOnBus (
  input  TICK_0,
  input  TICK_1,
  input  TICK_2,
  input  TICK_3,
  input  [7:0] INSTRUCTION,
  output INSTRUCTION_WRITE_ON_BUS,
  output INSTRUCTION_DEST,
  output RAM_WRITE_ON_BUS,
  output DA_CACHE_WRITE,
  output ACC_WRITE_ON_BUS,
  output RAM_WRITE,
  output DA_CACHE_WRITE_ON_BUS,
  output RESET_TC
);

  wire and_1_out, and_2_out, and_3_out, and_4_out, and_5_out, comparator_1_eq, comparator_2_eq;

  Comparator #(.mode("unsigned")) comparator_1 (.a(INSTRUCTION), .b(8'h3), .eq(comparator_1_eq));  // open: gt, lt
  Comparator #(.mode("unsigned")) comparator_2 (.a(INSTRUCTION), .b(8'h83), .eq(comparator_2_eq));  // open: gt, lt
  and and_1 (and_1_out, TICK_0, comparator_1_eq);
  and and_2 (and_2_out, TICK_1, comparator_1_eq);
  and and_3 (and_3_out, TICK_2, comparator_1_eq);
  and and_4 (and_4_out, TICK_3, comparator_1_eq);
  and and_5 (and_5_out, TICK_1, comparator_2_eq);
  or or_1 (INSTRUCTION_WRITE_ON_BUS, and_1_out, and_2_out, comparator_2_eq);
  or or_2 (INSTRUCTION_DEST, and_1_out, and_2_out, comparator_2_eq);
  or or_3 (RAM_WRITE_ON_BUS, and_1_out, and_2_out);
  or or_4 (DA_CACHE_WRITE, and_1_out, and_2_out);
  or or_5 (ACC_WRITE_ON_BUS, and_3_out, and_4_out, comparator_2_eq);
  or or_6 (RAM_WRITE, and_3_out, and_4_out, comparator_2_eq);
  or or_7 (DA_CACHE_WRITE_ON_BUS, and_3_out, and_4_out);
  or or_8 (RESET_TC, and_4_out, and_5_out);
endmodule

// 1HOT_TICK
module Counter (
  input  CLOCK,
  input  RESET,
  output TICK_0,
  output TICK_1,
  output TICK_2,
  output TICK_3,
  output TICK_4
);

  wire and_1_out, and_2_out, and_3_out, and_4_out, not_1_out, not_2_out, or_1_out, or_2_out;

  or or_1 (or_1_out, TICK_0, TICK_1, TICK_2, TICK_3, TICK_4);
  not not_1 (not_1_out, or_1_out);
  or or_2 (or_2_out, TICK_4, not_1_out, RESET);
  not not_2 (not_2_out, RESET);
  D_Flip_Flop d_ff_1 (.clk(CLOCK), .D(or_2_out), .Q(TICK_0), .en(1'b1));  // open: Qn, preset, reset
  and and_1 (and_1_out, TICK_0, not_2_out);
  D_Flip_Flop d_ff_2 (.clk(CLOCK), .D(and_1_out), .Q(TICK_1), .en(1'b1));  // open: Qn, preset, reset
  D_Flip_Flop d_ff_3 (.clk(CLOCK), .D(and_2_out), .Q(TICK_2), .en(1'b1));  // open: Qn, preset, reset
  and and_2 (and_2_out, TICK_1, not_2_out);
  and and_3 (and_3_out, TICK_2, not_2_out);
  D_Flip_Flop d_ff_4 (.clk(CLOCK), .D(and_3_out), .Q(TICK_3), .en(1'b1));  // open: Qn, preset, reset
  and and_4 (and_4_out, TICK_3, not_2_out);
  D_Flip_Flop d_ff_5 (.clk(CLOCK), .D(and_4_out), .Q(TICK_4), .en(1'b1));  // open: Qn, preset, reset
endmodule

module ROM (
);

  wire undriven;
  wire [7:0] IP_cache_q, IP_q;
  wire [15:0] rom_1_data;

  Counter_part IP (.Q(IP_q), .clk(undriven));  // open: load, D, count, carry, clr
  Register IP_cache (.D(IP_q), .Q(IP_cache_q), .clk(undriven));  // open: en, clr
  ROM_part #(.dataWidth(16)) rom_1 (.addr(IP_cache_q), .data(rom_1_data), .sel(1'b1));

  // Notes on the sheet:
  //   contents of rom_1 (hex, n*v repeats v):
  //   3402 3 2b02 103 1 203
endmodule

// CONTROLLER
module Controller (
  input  [7:0] INSTRUCTION,
  input  CLOCK,
  input  TICK0,
  input  TICK1,
  input  TICK2,
  input  TICK3,
  input  TICK4,
  input  EQUALS,
  input  GREATER_THAN,
  input  LESS_THAN,
  output RESET_TC,
  output [7:0] CTRL,
  output ACC_DEST,
  output ACC_SOURCE,
  output ACC_WRITE_ON_BUS,
  output ACC_WRITE,
  output ACC_CACHE_WRITE,
  output INSTRUCTION_DEST,
  output INSTRUCTION_WRITE_ON_BUS,
  output ARITHM_ADD,
  output ARITHM_SUB,
  output ARITHM_MUL,
  output ARITHM_DIV,
  output LOGIC_AND,
  output LOGIC_OR,
  output LOGIC_XOR,
  output LOGIC_INVERT,
  output IP_LOAD,
  output IP_SOURCE,
  output DA_CACHE_WRITE,
  output DA_CACHE_WRITE_ON_BUS
);

  wire n0e_0f_10_8e_8f_90_conditionalskip_1_instruction_dest,
       n0e_0f_10_8e_8f_90_conditionalskip_1_instruction_write_on_bus,
       n0e_0f_10_8e_8f_90_conditionalskip_1_ip_load, n0e_0f_10_8e_8f_90_conditionalskip_1_ram_write_on_bus,
       n0e_0f_10_8e_8f_90_conditionalskip_1_reset_tc, n0x0a_0b_0c_0d_8a_8b_8c_logic_1_acc_cache_write,
       n0x0a_0b_0c_0d_8a_8b_8c_logic_1_acc_write, n0x0a_0b_0c_0d_8a_8b_8c_logic_1_instruction_dest,
       n0x0a_0b_0c_0d_8a_8b_8c_logic_1_instruction_write_on_bus, n0x0a_0b_0c_0d_8a_8b_8c_logic_1_logic_and,
       n0x0a_0b_0c_0d_8a_8b_8c_logic_1_logic_inv, n0x0a_0b_0c_0d_8a_8b_8c_logic_1_logic_or,
       n0x0a_0b_0c_0d_8a_8b_8c_logic_1_logic_xor, n0x0a_0b_0c_0d_8a_8b_8c_logic_1_ram_write_on_bus,
       n0x0a_0b_0c_0d_8a_8b_8c_logic_1_reset_tc, n0x01_81_accload_1_acc_write,
       n0x01_81_accload_1_instruction_dest, n0x01_81_accload_1_instruction_write_on_bus,
       n0x01_81_accload_1_ram_write_on_bus, n0x01_81_accload_1_reset_tc,
       n0x03_83_accwriteonbus_1_acc_write_on_bus, n0x03_83_accwriteonbus_1_da_cache_write,
       n0x03_83_accwriteonbus_1_da_cache_write_on_bus, n0x03_83_accwriteonbus_1_instruction_dest,
       n0x03_83_accwriteonbus_1_instruction_write_on_bus, n0x03_83_accwriteonbus_1_ram_write,
       n0x03_83_accwriteonbus_1_ram_write_on_bus, n0x03_83_accwriteonbus_1_reset_tc,
       n0x04_05_06_07_84_85_86_87_arithmetic_1_acc_cache_write,
       n0x04_05_06_07_84_85_86_87_arithmetic_1_acc_write, n0x04_05_06_07_84_85_86_87_arithmetic_1_arithm_add,
       n0x04_05_06_07_84_85_86_87_arithmetic_1_arithm_div,
       n0x04_05_06_07_84_85_86_87_arithmetic_1_arithm_mul,
       n0x04_05_06_07_84_85_86_87_arithmetic_1_arithm_sub,
       n0x04_05_06_07_84_85_86_87_arithmetic_1_instruction_dest,
       n0x04_05_06_07_84_85_86_87_arithmetic_1_instruction_write_on_bus,
       n0x04_05_06_07_84_85_86_87_arithmetic_1_ram_write_on_bus,
       n0x04_05_06_07_84_85_86_87_arithmetic_1_reset_tc, n0x08_88_09_setip_1_acc_write_on_bus,
       n0x08_88_09_setip_1_instruction_dest, n0x08_88_09_setip_1_instruction_write_on_bus,
       n0x08_88_09_setip_1_ip_load, n0x08_88_09_setip_1_ip_source, n0x08_88_09_setip_1_ram_write_on_bus,
       n0x08_88_09_setip_1_reset_tc;

  _0x01_81_AccLoad u_0x01_81_accload_1 (
    .TICK_1(TICK1), .INSTRUCTION(INSTRUCTION), .RESET_TC(n0x01_81_accload_1_reset_tc),
    .ACC_WRITE(n0x01_81_accload_1_acc_write),
    .INSTRUCTION_WRITE_ON_BUS(n0x01_81_accload_1_instruction_write_on_bus),
    .RAM_WRITE_ON_BUS(n0x01_81_accload_1_ram_write_on_bus),
    .INSTRUCTION_DEST(n0x01_81_accload_1_instruction_dest));
  _0x03_83_AccWriteOnBus u_0x03_83_accwriteonbus_1 (
    .TICK_0(TICK0), .TICK_1(TICK1), .TICK_2(TICK2), .TICK_3(TICK3), .INSTRUCTION(INSTRUCTION),
    .INSTRUCTION_WRITE_ON_BUS(n0x03_83_accwriteonbus_1_instruction_write_on_bus),
    .INSTRUCTION_DEST(n0x03_83_accwriteonbus_1_instruction_dest),
    .RAM_WRITE_ON_BUS(n0x03_83_accwriteonbus_1_ram_write_on_bus),
    .DA_CACHE_WRITE(n0x03_83_accwriteonbus_1_da_cache_write),
    .ACC_WRITE_ON_BUS(n0x03_83_accwriteonbus_1_acc_write_on_bus),
    .RAM_WRITE(n0x03_83_accwriteonbus_1_ram_write),
    .DA_CACHE_WRITE_ON_BUS(n0x03_83_accwriteonbus_1_da_cache_write_on_bus),
    .RESET_TC(n0x03_83_accwriteonbus_1_reset_tc));
  _0x04_05_06_07_84_85_86_87_Arithmetic u_0x04_05_06_07_84_85_86_87_arithmetic_1 (
    .TICK_0(TICK0), .TICK_1(TICK1), .INSTRUCTION(INSTRUCTION),
    .ARITHM_ADD(n0x04_05_06_07_84_85_86_87_arithmetic_1_arithm_add),
    .ARITHM_SUB(n0x04_05_06_07_84_85_86_87_arithmetic_1_arithm_sub),
    .ARITHM_MUL(n0x04_05_06_07_84_85_86_87_arithmetic_1_arithm_mul),
    .ARITHM_DIV(n0x04_05_06_07_84_85_86_87_arithmetic_1_arithm_div),
    .ACC_CACHE_WRITE(n0x04_05_06_07_84_85_86_87_arithmetic_1_acc_cache_write),
    .ACC_WRITE(n0x04_05_06_07_84_85_86_87_arithmetic_1_acc_write),
    .RESET_TC(n0x04_05_06_07_84_85_86_87_arithmetic_1_reset_tc),
    .INSTRUCTION_WRITE_ON_BUS(n0x04_05_06_07_84_85_86_87_arithmetic_1_instruction_write_on_bus),
    .INSTRUCTION_DEST(n0x04_05_06_07_84_85_86_87_arithmetic_1_instruction_dest),
    .RAM_WRITE_ON_BUS(n0x04_05_06_07_84_85_86_87_arithmetic_1_ram_write_on_bus));
  _0x08_88_09_SetIP u_0x08_88_09_setip_1 (
    .TICK_1(TICK1), .INSTRUCTION(INSTRUCTION), .RESET_TC(n0x08_88_09_setip_1_reset_tc),
    .INSTRUCTION_WRITE_ON_BUS(n0x08_88_09_setip_1_instruction_write_on_bus),
    .IP_LOAD(n0x08_88_09_setip_1_ip_load), .IP_SOURCE(n0x08_88_09_setip_1_ip_source),
    .RAM_WRITE_ON_BUS(n0x08_88_09_setip_1_ram_write_on_bus),
    .INSTRUCTION_DEST(n0x08_88_09_setip_1_instruction_dest),
    .ACC_WRITE_ON_BUS(n0x08_88_09_setip_1_acc_write_on_bus));
  _0x0a_0b_0c_0d_8a_8b_8c_Logic u_0x0a_0b_0c_0d_8a_8b_8c_logic_1 (
    .TICK_0(TICK0), .TICK_1(TICK1), .INSTRUCTION(INSTRUCTION),
    .LOGIC_AND(n0x0a_0b_0c_0d_8a_8b_8c_logic_1_logic_and),
    .LOGIC_OR(n0x0a_0b_0c_0d_8a_8b_8c_logic_1_logic_or),
    .LOGIC_XOR(n0x0a_0b_0c_0d_8a_8b_8c_logic_1_logic_xor),
    .LOGIC_INV(n0x0a_0b_0c_0d_8a_8b_8c_logic_1_logic_inv),
    .ACC_CACHE_WRITE(n0x0a_0b_0c_0d_8a_8b_8c_logic_1_acc_cache_write),
    .ACC_WRITE(n0x0a_0b_0c_0d_8a_8b_8c_logic_1_acc_write),
    .RESET_TC(n0x0a_0b_0c_0d_8a_8b_8c_logic_1_reset_tc),
    .INSTRUCTION_WRITE_ON_BUS(n0x0a_0b_0c_0d_8a_8b_8c_logic_1_instruction_write_on_bus),
    .INSTRUCTION_DEST(n0x0a_0b_0c_0d_8a_8b_8c_logic_1_instruction_dest),
    .RAM_WRITE_ON_BUS(n0x0a_0b_0c_0d_8a_8b_8c_logic_1_ram_write_on_bus));
  _0e_0f_10_8e_8f_90_ConditionalSkip u_0e_0f_10_8e_8f_90_conditionalskip_1 (
    .TICK_1(TICK1), .INSTRUCTION(INSTRUCTION), .LESS_THAN(LESS_THAN), .EQUALS(EQUALS),
    .GREATER_THAN(GREATER_THAN), .IP_LOAD(n0e_0f_10_8e_8f_90_conditionalskip_1_ip_load),
    .INSTRUCTION_WRITE_ON_BUS(n0e_0f_10_8e_8f_90_conditionalskip_1_instruction_write_on_bus),
    .RESET_TC(n0e_0f_10_8e_8f_90_conditionalskip_1_reset_tc),
    .INSTRUCTION_DEST(n0e_0f_10_8e_8f_90_conditionalskip_1_instruction_dest),
    .RAM_WRITE_ON_BUS(n0e_0f_10_8e_8f_90_conditionalskip_1_ram_write_on_bus));
  or u_RESET_TC (RESET_TC, n0e_0f_10_8e_8f_90_conditionalskip_1_reset_tc, n0x01_81_accload_1_reset_tc, n0x03_83_accwriteonbus_1_reset_tc, n0x08_88_09_setip_1_reset_tc, n0x0a_0b_0c_0d_8a_8b_8c_logic_1_reset_tc, n0x04_05_06_07_84_85_86_87_arithmetic_1_reset_tc);
  buf or_1 (CTRL[0], n0x03_83_accwriteonbus_1_ram_write);  // OR_Gate
  or or_2 (CTRL[1], n0e_0f_10_8e_8f_90_conditionalskip_1_ram_write_on_bus, n0x01_81_accload_1_ram_write_on_bus, n0x04_05_06_07_84_85_86_87_arithmetic_1_ram_write_on_bus, n0x03_83_accwriteonbus_1_ram_write_on_bus, n0x0a_0b_0c_0d_8a_8b_8c_logic_1_ram_write_on_bus, n0x08_88_09_setip_1_ram_write_on_bus);
  buf or_3 (ACC_DEST, 1'b0);  // OR_Gate
  buf or_4 (ACC_SOURCE, 1'b0);  // OR_Gate
  or or_5 (ACC_WRITE_ON_BUS, n0x08_88_09_setip_1_acc_write_on_bus, n0x03_83_accwriteonbus_1_acc_write_on_bus);
  or or_6 (ACC_WRITE, n0x01_81_accload_1_acc_write, n0x04_05_06_07_84_85_86_87_arithmetic_1_acc_write, n0x0a_0b_0c_0d_8a_8b_8c_logic_1_acc_write);
  or or_7 (ACC_CACHE_WRITE, n0x04_05_06_07_84_85_86_87_arithmetic_1_acc_cache_write, n0x0a_0b_0c_0d_8a_8b_8c_logic_1_acc_cache_write);
  or or_8 (INSTRUCTION_DEST, n0e_0f_10_8e_8f_90_conditionalskip_1_instruction_dest, n0x01_81_accload_1_instruction_dest, n0x03_83_accwriteonbus_1_instruction_dest, n0x08_88_09_setip_1_instruction_dest, n0x0a_0b_0c_0d_8a_8b_8c_logic_1_instruction_dest, n0x04_05_06_07_84_85_86_87_arithmetic_1_instruction_dest);
  or or_9 (INSTRUCTION_WRITE_ON_BUS, n0x04_05_06_07_84_85_86_87_arithmetic_1_instruction_write_on_bus, n0x01_81_accload_1_instruction_write_on_bus, n0x03_83_accwriteonbus_1_instruction_write_on_bus, n0x08_88_09_setip_1_instruction_write_on_bus, n0x0a_0b_0c_0d_8a_8b_8c_logic_1_instruction_write_on_bus, n0e_0f_10_8e_8f_90_conditionalskip_1_instruction_write_on_bus);
  buf or_10 (ARITHM_ADD, n0x04_05_06_07_84_85_86_87_arithmetic_1_arithm_add);  // OR_Gate
  buf or_11 (ARITHM_SUB, n0x04_05_06_07_84_85_86_87_arithmetic_1_arithm_sub);  // OR_Gate
  buf or_12 (ARITHM_MUL, n0x04_05_06_07_84_85_86_87_arithmetic_1_arithm_mul);  // OR_Gate
  buf or_13 (ARITHM_DIV, n0x04_05_06_07_84_85_86_87_arithmetic_1_arithm_div);  // OR_Gate
  buf or_14 (LOGIC_AND, n0x0a_0b_0c_0d_8a_8b_8c_logic_1_logic_and);  // OR_Gate
  buf or_15 (LOGIC_OR, n0x0a_0b_0c_0d_8a_8b_8c_logic_1_logic_or);  // OR_Gate
  buf or_16 (LOGIC_XOR, n0x0a_0b_0c_0d_8a_8b_8c_logic_1_logic_xor);  // OR_Gate
  buf or_17 (LOGIC_INVERT, n0x0a_0b_0c_0d_8a_8b_8c_logic_1_logic_inv);  // OR_Gate
  or or_18 (IP_LOAD, n0x08_88_09_setip_1_ip_load, n0e_0f_10_8e_8f_90_conditionalskip_1_ip_load);
  buf or_19 (IP_SOURCE, n0x08_88_09_setip_1_ip_source);  // OR_Gate
  buf or_20 (DA_CACHE_WRITE, n0x03_83_accwriteonbus_1_da_cache_write);  // OR_Gate
  buf or_21 (DA_CACHE_WRITE_ON_BUS, n0x03_83_accwriteonbus_1_da_cache_write_on_bus);  // OR_Gate

  assign CTRL[2] = CLOCK;

  // Notes on the sheet:
  //   CTRL_READ_FROM_BUS
  //   CTRL_WRITE_ON_BUS
  //   (0 -> DATA, 1 -> ADDRESS)
endmodule

// Arithmetic
module _0x04_05_06_07_84_85_86_87_Arithmetic (
  input  TICK_0,
  input  TICK_1,
  input  [7:0] INSTRUCTION,
  output ARITHM_ADD,
  output ARITHM_SUB,
  output ARITHM_MUL,
  output ARITHM_DIV,
  output ACC_CACHE_WRITE,
  output ACC_WRITE,
  output RESET_TC,
  output INSTRUCTION_WRITE_ON_BUS,
  output INSTRUCTION_DEST,
  output RAM_WRITE_ON_BUS
);

  wire [6:0] bit_extender_1_out;

  Bit_Extender #(.out_width(7)) bit_extender_1 (.in(INSTRUCTION), .out(bit_extender_1_out));
  Comparator #(.width(7), .mode("unsigned")) comparator_1 (
    .a(bit_extender_1_out), .b(7'b0000100), .eq(ARITHM_ADD));  // open: gt, lt
  Comparator #(.width(7), .mode("unsigned")) comparator_2 (
    .a(bit_extender_1_out), .b(7'b0000101), .eq(ARITHM_SUB));  // open: gt, lt
  Comparator #(.width(7), .mode("unsigned")) comparator_3 (
    .a(bit_extender_1_out), .b(7'b0000110), .eq(ARITHM_MUL));  // open: gt, lt
  Comparator #(.width(7), .mode("unsigned")) comparator_4 (
    .a(bit_extender_1_out), .b(7'b0000111), .eq(ARITHM_DIV));  // open: gt, lt
  or or_1 (INSTRUCTION_WRITE_ON_BUS, ARITHM_ADD, ARITHM_SUB, ARITHM_MUL, ARITHM_DIV);
  and and_1 (ACC_CACHE_WRITE, TICK_0, INSTRUCTION_WRITE_ON_BUS);
  and and_2 (ACC_WRITE, TICK_1, INSTRUCTION_WRITE_ON_BUS);
  and and_3 (INSTRUCTION_DEST, ~INSTRUCTION[7], INSTRUCTION_WRITE_ON_BUS);  // AND_Gate

  assign RAM_WRITE_ON_BUS = INSTRUCTION_DEST;
  assign RESET_TC = ACC_WRITE;

  // Notes on the sheet:
  //   (IMMEDIATE)
endmodule

// Set IP
module _0x08_88_09_SetIP (
  input  TICK_1,
  input  [7:0] INSTRUCTION,
  output RESET_TC,
  output INSTRUCTION_WRITE_ON_BUS,
  output IP_LOAD,
  output IP_SOURCE,
  output RAM_WRITE_ON_BUS,
  output INSTRUCTION_DEST,
  output ACC_WRITE_ON_BUS
);

  wire and_1_out, and_2_out;
  wire [6:0] bit_extender_1_out;

  Bit_Extender #(.out_width(7)) bit_extender_1 (.in(INSTRUCTION), .out(bit_extender_1_out));
  Comparator #(.width(7), .mode("unsigned")) comparator_1 (
    .a(bit_extender_1_out), .b(7'b0001000), .eq(INSTRUCTION_WRITE_ON_BUS));  // open: gt, lt
  Comparator #(.mode("unsigned")) comparator_2 (.a(INSTRUCTION), .b(8'h9), .eq(ACC_WRITE_ON_BUS));  // open: gt, lt
  and and_1 (and_1_out, TICK_1, INSTRUCTION_WRITE_ON_BUS);
  and and_2 (and_2_out, TICK_1, ACC_WRITE_ON_BUS);
  or or_1 (RESET_TC, and_1_out, and_2_out);
  and and_3 (INSTRUCTION_DEST, ~INSTRUCTION[7], INSTRUCTION_WRITE_ON_BUS);  // AND_Gate
  or or_2 (IP_LOAD, INSTRUCTION_WRITE_ON_BUS, ACC_WRITE_ON_BUS);

  assign IP_SOURCE = IP_LOAD;
  assign RAM_WRITE_ON_BUS = INSTRUCTION_DEST;
endmodule

// AND
module BITWISE_AND (
  input  [7:0] in_1,
  input  [7:0] in_2,
  output [7:0] out_3
);

  and and_1 (out_3[0], in_1[0], in_2[0]);
  and and_2 (out_3[1], in_1[1], in_2[1]);
  and and_3 (out_3[2], in_1[2], in_2[2]);
  and and_4 (out_3[3], in_1[3], in_2[3]);
  and and_5 (out_3[4], in_1[4], in_2[4]);
  and and_6 (out_3[5], in_1[5], in_2[5]);
  and and_7 (out_3[6], in_1[6], in_2[6]);
  and and_8 (out_3[7], in_1[7], in_2[7]);
endmodule

// OR
module BITWISE_OR (
  input  [7:0] in_1,
  input  [7:0] in_2,
  output [7:0] out_3
);

  or or_1 (out_3[0], in_1[0], in_2[0]);
  or or_2 (out_3[1], in_1[1], in_2[1]);
  or or_3 (out_3[2], in_1[2], in_2[2]);
  or or_4 (out_3[3], in_1[3], in_2[3]);
  or or_5 (out_3[4], in_1[4], in_2[4]);
  or or_6 (out_3[5], in_1[5], in_2[5]);
  or or_7 (out_3[6], in_1[6], in_2[6]);
  or or_8 (out_3[7], in_1[7], in_2[7]);
endmodule

// XOR
module BITWISE_XOR (
  input  [7:0] in_1,
  input  [7:0] in_2,
  output [7:0] out_3
);

  xor xor_1 (out_3[0], in_1[0], in_2[0]);
  xor xor_2 (out_3[1], in_1[1], in_2[1]);
  xor xor_3 (out_3[2], in_1[2], in_2[2]);
  xor xor_4 (out_3[3], in_1[3], in_2[3]);
  xor xor_5 (out_3[4], in_1[4], in_2[4]);
  xor xor_6 (out_3[5], in_1[5], in_2[5]);
  xor xor_7 (out_3[6], in_1[6], in_2[6]);
  xor xor_8 (out_3[7], in_1[7], in_2[7]);
endmodule

// Logic
module _0x0a_0b_0c_0d_8a_8b_8c_Logic (
  input  TICK_0,
  input  TICK_1,
  input  [7:0] INSTRUCTION,
  output LOGIC_AND,
  output LOGIC_OR,
  output LOGIC_XOR,
  output LOGIC_INV,
  output ACC_CACHE_WRITE,
  output ACC_WRITE,
  output RESET_TC,
  output INSTRUCTION_WRITE_ON_BUS,
  output INSTRUCTION_DEST,
  output RAM_WRITE_ON_BUS
);

  wire [6:0] bit_extender_1_out;

  Bit_Extender #(.out_width(7)) bit_extender_1 (.in(INSTRUCTION), .out(bit_extender_1_out));
  Comparator #(.width(7), .mode("unsigned")) comparator_1 (
    .a(bit_extender_1_out), .b(7'b0001010), .eq(LOGIC_AND));  // open: gt, lt
  Comparator #(.width(7), .mode("unsigned")) comparator_2 (
    .a(bit_extender_1_out), .b(7'b0001011), .eq(LOGIC_OR));  // open: gt, lt
  Comparator #(.width(7), .mode("unsigned")) comparator_3 (
    .a(bit_extender_1_out), .b(7'b0001100), .eq(LOGIC_XOR));  // open: gt, lt
  Comparator #(.width(7), .mode("unsigned")) comparator_4 (
    .a(bit_extender_1_out), .b(7'b0001101), .eq(LOGIC_INV));  // open: gt, lt
  or or_1 (INSTRUCTION_WRITE_ON_BUS, LOGIC_AND, LOGIC_OR, LOGIC_XOR, LOGIC_INV);
  and and_1 (ACC_CACHE_WRITE, TICK_0, INSTRUCTION_WRITE_ON_BUS);
  and and_2 (ACC_WRITE, TICK_1, INSTRUCTION_WRITE_ON_BUS);
  and and_3 (INSTRUCTION_DEST, ~INSTRUCTION[7], INSTRUCTION_WRITE_ON_BUS);  // AND_Gate

  assign RAM_WRITE_ON_BUS = INSTRUCTION_DEST;
  assign RESET_TC = ACC_WRITE;

  // Notes on the sheet:
  //   (IMMEDIATE)
endmodule

// INV
module _8BIT_INVERTER (
  input  [7:0] in_1,
  output [7:0] out_2
);

  not not_1 (out_2[0], in_1[0]);
  not not_2 (out_2[1], in_1[1]);
  not not_3 (out_2[2], in_1[2]);
  not not_4 (out_2[3], in_1[3]);
  not not_5 (out_2[4], in_1[4]);
  not not_6 (out_2[5], in_1[5]);
  not not_7 (out_2[6], in_1[6]);
  not not_8 (out_2[7], in_1[7]);
endmodule

// ConditionalSkip
module _0e_0f_10_8e_8f_90_ConditionalSkip (
  input  TICK_1,
  input  [7:0] INSTRUCTION,
  input  LESS_THAN,
  input  EQUALS,
  input  GREATER_THAN,
  output IP_LOAD,
  output INSTRUCTION_WRITE_ON_BUS,
  output RESET_TC,
  output INSTRUCTION_DEST,
  output RAM_WRITE_ON_BUS
);

  wire and_2_out, and_3_out, and_4_out, comparator_1_eq, comparator_2_eq, comparator_3_eq, or_2_out;
  wire [6:0] bit_extender_1_out;

  Bit_Extender #(.out_width(7)) bit_extender_1 (.in(INSTRUCTION), .out(bit_extender_1_out));
  Comparator #(.width(7), .mode("unsigned")) comparator_1 (
    .a(bit_extender_1_out), .b(7'b0001110), .eq(comparator_1_eq));  // open: gt, lt
  Comparator #(.width(7), .mode("unsigned")) comparator_2 (
    .a(bit_extender_1_out), .b(7'b0001111), .eq(comparator_2_eq));  // open: gt, lt
  Comparator #(.width(7), .mode("unsigned")) comparator_3 (
    .a(bit_extender_1_out), .b(7'b0010000), .eq(comparator_3_eq));  // open: gt, lt
  or or_1 (INSTRUCTION_WRITE_ON_BUS, comparator_1_eq, comparator_2_eq, comparator_3_eq);
  and and_1 (INSTRUCTION_DEST, ~INSTRUCTION[7], INSTRUCTION_WRITE_ON_BUS);  // AND_Gate
  and and_2 (and_2_out, comparator_1_eq, LESS_THAN);
  and and_3 (and_3_out, comparator_2_eq, EQUALS);
  and and_4 (and_4_out, comparator_3_eq, GREATER_THAN);
  or or_2 (or_2_out, and_2_out, and_3_out, and_4_out);
  and and_5 (IP_LOAD, TICK_1, or_2_out);
  and and_6 (RESET_TC, TICK_1, INSTRUCTION_WRITE_ON_BUS);

  assign RAM_WRITE_ON_BUS = INSTRUCTION_DEST;

  // Notes on the sheet:
  //   (IMMEDIATE)
endmodule
