// Logisim project CPU_neumann.circ as structural Verilog: 18 circuits, main circuit main
module main (
);

  wire alu_1_at_least_1, Buffer_delay_out, Clock_out, controller_1_cache0_write, controller_1_cache1_write,
       controller_1_da_cache_write, controller_1_da_cache_write_on_bus, controller_1_dd_cache_write,
       controller_1_dd_cache_write_on_bus, controller_1_instr_cache_write, controller_1_ip_source,
       controller_1_ip_write, controller_1_ip_write_on_ab, controller_1_ip_write_on_db,
       controller_1_opselect0, controller_1_opselect1, controller_1_opselect2, controller_1_opselect3,
       controller_1_opwrite, controller_1_reset, controller_1_status_write_on_bus, counter_1_tick_0,
       counter_1_tick_1, counter_1_tick_2, counter_1_tick_3, counter_1_tick_4, counter_1_tick_5,
       counter_1_tick_6, displayctrl_1_clock, displayctrl_1_select, or_1_out;
  wire [6:0] displayctrl_1_data_2;
  wire [7:0] adder_1_out, alu_1_data_2, controlled_buffer_2_out, controller_1_ctrl, DA_CACHE_q, DD_CACHE_q,
       INSTR_CACHE_q, IP_q, multiplexer_1_out;

  Counter counter_1 (
    .START(1'b1), .CLOCK(Clock_out), .RESET(controller_1_reset), .TICK_0(counter_1_tick_0),
    .TICK_1(counter_1_tick_1), .TICK_2(counter_1_tick_2), .TICK_3(counter_1_tick_3),
    .TICK_4(counter_1_tick_4), .TICK_5(counter_1_tick_5), .TICK_6(counter_1_tick_6));
  Clock Clock (.out(Clock_out));
  BUFFER_DELAY Buffer_delay (.IN(Clock_out), .OUT(Buffer_delay_out));
  Controller controller_1 (
    .INSTRUCTION(INSTR_CACHE_q), .CLOCK(Buffer_delay_out), .TICK0(counter_1_tick_0),
    .TICK1(counter_1_tick_1), .TICK2(counter_1_tick_2), .TICK3(counter_1_tick_3), .TICK4(counter_1_tick_4),
    .TICK5(counter_1_tick_5), .TICK6(counter_1_tick_6), ._0(alu_1_at_least_1),
    .IP_WRITE_ON_AB(controller_1_ip_write_on_ab), .INSTR_CACHE_WRITE(controller_1_instr_cache_write),
    .RESET(controller_1_reset), .CTRL(controller_1_ctrl), .CACHE0_WRITE(controller_1_cache0_write),
    .CACHE1_WRITE(controller_1_cache1_write), .IP_WRITE(controller_1_ip_write),
    .DA_CACHE_WRITE(controller_1_da_cache_write), .DA_CACHE_WRITE_ON_BUS(controller_1_da_cache_write_on_bus),
    .DD_CACHE_WRITE(controller_1_dd_cache_write), .DD_CACHE_WRITE_ON_BUS(controller_1_dd_cache_write_on_bus),
    .OPWRITE(controller_1_opwrite), .OPSELECT0(controller_1_opselect0), .OPSELECT1(controller_1_opselect1),
    .OPSELECT2(controller_1_opselect2), .OPSELECT3(controller_1_opselect3),
    .IP_SOURCE(controller_1_ip_source), .STATUS_WRITE_ON_BUS(controller_1_status_write_on_bus),
    .IP_WRITE_ON_DB(controller_1_ip_write_on_db));
  Multiplexer #(.width(8)) multiplexer_1 (
    .in0(adder_1_out), .in1(alu_1_data_2), .out(multiplexer_1_out), .sel(controller_1_ip_source));  // open: en
  Register IP (.D(multiplexer_1_out), .en(or_1_out), .Q(IP_q), .clk(Buffer_delay_out));  // open: clr
  or or_1 (or_1_out, controller_1_reset, controller_1_ip_write);
  Register INSTR_CACHE (
    .D(alu_1_data_2), .en(controller_1_instr_cache_write), .Q(INSTR_CACHE_q), .clk(Buffer_delay_out));  // open: clr
  Adder adder_1 (.a(8'h1), .b(IP_q), .out(adder_1_out));  // open: cin, cout
  ALU alu_1 (
    .OPWRITE(controller_1_opwrite), .OPSELECT0(controller_1_opselect0), .OPSELECT1(controller_1_opselect1),
    .OPSELECT2(controller_1_opselect2), .OPSELECT3(controller_1_opselect3), .DATA(alu_1_data_2),
    .CLOCK(Buffer_delay_out), .CACHE0_WRITE(controller_1_cache0_write),
    .CACHE1_WRITE(controller_1_cache1_write), .STATUS_WRITE_ON_BUS(controller_1_status_write_on_bus),
    .AT_LEAST_1(alu_1_at_least_1), .DATA_2(alu_1_data_2));
  assign alu_1_data_2 = controller_1_ip_write_on_db ? adder_1_out : 8'bz;  // Controlled_Buffer controlled_buffer_1
  Pull_Resistor pull_resistor_1 (.node(alu_1_data_2));
  assign controlled_buffer_2_out = controller_1_ip_write_on_ab ? IP_q : 8'bz;  // Controlled_Buffer controlled_buffer_2
  Register DD_CACHE (
    .D(alu_1_data_2), .en(controller_1_dd_cache_write), .Q(DD_CACHE_q), .clk(Buffer_delay_out));  // open: clr
  assign alu_1_data_2 = controller_1_dd_cache_write_on_bus ? DD_CACHE_q : 8'bz;  // Controlled_Buffer controlled_buffer_3
  Register DA_CACHE (
    .D(alu_1_data_2), .en(controller_1_da_cache_write), .Q(DA_CACHE_q), .clk(Buffer_delay_out));  // open: clr
  assign controlled_buffer_2_out = controller_1_da_cache_write_on_bus ? DA_CACHE_q : 8'bz;  // Controlled_Buffer controlled_buffer_4
  Pull_Resistor pull_resistor_2 (.node(controlled_buffer_2_out));
  Pull_Resistor pull_resistor_3 (.node(controller_1_ctrl));
  RAM ram_1 (
    .ADDRESS(controlled_buffer_2_out), .DATA(alu_1_data_2), .CONTROL(controller_1_ctrl), .DATA_2(alu_1_data_2));
  DISPLAYCTRL displayctrl_1 (
    .CTRL(controller_1_ctrl), .DATA(alu_1_data_2), .ADDRESS(controlled_buffer_2_out),
    .CLOCK(displayctrl_1_clock), .DATA_2(displayctrl_1_data_2), .SELECT(displayctrl_1_select));
  TTY tty_1 (.data(displayctrl_1_data_2), .clk(displayctrl_1_clock), .we(displayctrl_1_select));  // open: clr

  // Notes on the sheet:
  //   DATA_BUS
  //   ADDRESS_BUS
  //   Memory devices
  //   CONTROL_BUS
endmodule

module ALU (
  input  OPWRITE,
  input  OPSELECT0,
  input  OPSELECT1,
  input  OPSELECT2,
  input  OPSELECT3,
  input  [7:0] DATA,
  input  CLOCK,
  input  CACHE0_WRITE,
  input  CACHE1_WRITE,
  input  STATUS_WRITE_ON_BUS,
  output AT_LEAST_1,
  output [7:0] DATA_2
);

  wire adder_1_cout, and_1_out, and_2_out, and_3_out, and_4_out, and_5_out, and_6_out, and_7_out, and_8_out,
       and_9_out, and_10_out, and_11_out, and_12_out, and_13_out, and_14_out, and_15_out, and_16_out,
       and_17_out, and_19_out, and_20_out, or_2_out, or_3_out, subtractor_1_bout;
  wire [3:0] or_4_out;
  wire [7:0] adder_1_out, ALU_CACHE_0_q, ALU_CACHE_1_q, bitwise_and_1_out_3, bitwise_or_1_out_3,
       bitwise_xor_1_out_3, divider_1_out, divider_1_rem, multiplier_1_cout, multiplier_1_out,
       n8bit_inverter_1_out_2, STATUS_q, subtractor_1_out;

  Register ALU_CACHE_0 (.D(DATA), .en(CACHE0_WRITE), .Q(ALU_CACHE_0_q), .clk(CLOCK));  // open: clr
  Register ALU_CACHE_1 (.D(DATA), .en(CACHE1_WRITE), .Q(ALU_CACHE_1_q), .clk(CLOCK));  // open: clr
  or or_1 (AT_LEAST_1, ALU_CACHE_0_q[0], ALU_CACHE_0_q[1], ALU_CACHE_0_q[2], ALU_CACHE_0_q[3], ALU_CACHE_0_q[4], ALU_CACHE_0_q[5], ALU_CACHE_0_q[6], ALU_CACHE_0_q[7]);
  and and_1 (and_1_out, ~OPSELECT2, ~OPSELECT1, ~OPSELECT0);  // AND_Gate
  and and_2 (and_2_out, ~OPSELECT2, ~OPSELECT1, OPSELECT0);  // AND_Gate
  and and_3 (and_3_out, ~OPSELECT2, OPSELECT1, ~OPSELECT0);  // AND_Gate
  and and_4 (and_4_out, ~OPSELECT2, OPSELECT1, OPSELECT0);  // AND_Gate
  and and_5 (and_5_out, OPSELECT2, ~OPSELECT1, ~OPSELECT0);  // AND_Gate
  and and_6 (and_6_out, OPSELECT2, ~OPSELECT1, OPSELECT0);  // AND_Gate
  and and_7 (and_7_out, OPSELECT2, OPSELECT1, ~OPSELECT0);  // AND_Gate
  and and_8 (and_8_out, OPSELECT2, OPSELECT1, OPSELECT0);
  and and_9 (and_9_out, OPWRITE, and_1_out);
  and and_10 (and_10_out, OPWRITE, and_2_out);
  and and_11 (and_11_out, OPWRITE, and_3_out);
  and and_12 (and_12_out, OPWRITE, and_4_out);
  and and_13 (and_13_out, OPWRITE, and_5_out);
  and and_14 (and_14_out, OPWRITE, and_6_out);
  and and_15 (and_15_out, OPWRITE, and_7_out);
  and and_16 (and_16_out, OPWRITE, and_8_out);
  assign DATA_2 = and_9_out ? adder_1_out : 8'bz;  // Controlled_Buffer controlled_buffer_1
  Adder adder_1 (.a(ALU_CACHE_0_q), .b(ALU_CACHE_1_q), .out(adder_1_out), .cout(adder_1_cout));  // open: cin
  assign DATA_2 = and_10_out ? subtractor_1_out : 8'bz;  // Controlled_Buffer controlled_buffer_2
  Subtractor subtractor_1 (
    .a(ALU_CACHE_0_q), .b(ALU_CACHE_1_q), .out(subtractor_1_out), .bout(subtractor_1_bout));  // open: bin
  Multiplier multiplier_1 (
    .a(ALU_CACHE_0_q), .b(ALU_CACHE_1_q), .out(multiplier_1_out), .cout(multiplier_1_cout));  // open: cin
  assign DATA_2 = and_11_out ? multiplier_1_out : 8'bz;  // Controlled_Buffer controlled_buffer_3
  assign DATA_2 = and_12_out ? divider_1_out : 8'bz;  // Controlled_Buffer controlled_buffer_4
  Divider divider_1 (.a(ALU_CACHE_0_q), .b(ALU_CACHE_1_q), .out(divider_1_out), .rem(divider_1_rem));  // open: upper
  assign DATA_2 = and_13_out ? bitwise_and_1_out_3 : 8'bz;  // Controlled_Buffer controlled_buffer_5
  BITWISE_AND bitwise_and_1 (.in_1(ALU_CACHE_0_q), .in_2(ALU_CACHE_1_q), .out_3(bitwise_and_1_out_3));
  assign DATA_2 = and_14_out ? bitwise_or_1_out_3 : 8'bz;  // Controlled_Buffer controlled_buffer_6
  BITWISE_OR bitwise_or_1 (.in_1(ALU_CACHE_0_q), .in_2(ALU_CACHE_1_q), .out_3(bitwise_or_1_out_3));
  BITWISE_XOR bitwise_xor_1 (.in_1(ALU_CACHE_0_q), .in_2(ALU_CACHE_1_q), .out_3(bitwise_xor_1_out_3));
  assign DATA_2 = and_15_out ? bitwise_xor_1_out_3 : 8'bz;  // Controlled_Buffer controlled_buffer_7
  assign DATA_2 = and_16_out ? n8bit_inverter_1_out_2 : 8'bz;  // Controlled_Buffer controlled_buffer_8
  _8BIT_INVERTER u_8bit_inverter_1 (.in_1(ALU_CACHE_0_q), .out_2(n8bit_inverter_1_out_2));
  and and_17 (and_17_out, adder_1_cout, and_1_out);
  and and_18 (or_4_out[3], subtractor_1_bout, and_2_out);
  or or_2 (or_2_out, multiplier_1_cout[0], multiplier_1_cout[1], multiplier_1_cout[2], multiplier_1_cout[3], multiplier_1_cout[4], multiplier_1_cout[5], multiplier_1_cout[6], multiplier_1_cout[7]);
  or or_3 (or_3_out, divider_1_rem[0], divider_1_rem[1], divider_1_rem[2], divider_1_rem[3], divider_1_rem[4], divider_1_rem[5], divider_1_rem[6], divider_1_rem[7]);
  and and_19 (and_19_out, or_2_out, and_3_out);
  and and_20 (and_20_out, or_3_out, and_4_out);
  or or_4 (or_4_out[0], and_17_out, and_19_out, and_20_out);
  nor nor_1 (or_4_out[1], DATA_2[0], DATA_2[1], DATA_2[2], DATA_2[3], DATA_2[4], DATA_2[5], DATA_2[6], DATA_2[7]);
  xnor even_parity_1 (or_4_out[2], DATA_2[7], DATA_2[6], DATA_2[5], DATA_2[4], DATA_2[3], DATA_2[2], DATA_2[1], DATA_2[0]);
  Register STATUS (.D({4'b0000, or_4_out}), .en(OPWRITE), .Q(STATUS_q), .clk(CLOCK));  // open: clr
  assign DATA_2 = STATUS_WRITE_ON_BUS ? STATUS_q : 8'bz;  // Controlled_Buffer controlled_buffer_9

  // Notes on the sheet:
  //   0 ADD, 1 SUB, 2 MUL, 3 DIV, 4 AND, 5 OR, 6 XOR, 7 INV
endmodule

module RAM (
  input  [7:0] ADDRESS,
  input  [7:0] DATA,
  input  [7:0] CONTROL,
  output [7:0] DATA_2
);

  wire and_1_out, and_2_out, not_1_out;
  wire [6:0] bit_extender_1_out;
  wire [7:0] ram_1_data;

  not not_1 (not_1_out, ADDRESS[7]);
  Bit_Extender #(.out_width(7)) bit_extender_1 (.in(ADDRESS), .out(bit_extender_1_out));
  and and_1 (and_1_out, not_1_out, CONTROL[0]);
  RAM_part #(.addrWidth(7), .bus("separate")) ram_1 (
    .addr(bit_extender_1_out), .din(DATA), .data(ram_1_data), .str(and_1_out), .sel(1'b1), .clk(CONTROL[2]),
    .ld(1'b1));  // open: clr
  and and_2 (and_2_out, not_1_out, CONTROL[1]);
  assign DATA_2 = and_2_out ? ram_1_data : 8'bz;  // Controlled_Buffer controlled_buffer_1
endmodule

// 1HOT_TICK
module Counter (
  input  START,
  input  CLOCK,
  input  RESET,
  output TICK_0,
  output TICK_1,
  output TICK_2,
  output TICK_3,
  output TICK_4,
  output TICK_5,
  output TICK_6
);

  wire and_1_out, and_2_out, and_3_out, and_4_out, and_5_out, and_6_out, and_7_out, nor_1_out, not_1_out,
       or_1_out;

  nor nor_1 (nor_1_out, TICK_0, TICK_1, TICK_2, TICK_3, TICK_4, TICK_5, TICK_6);
  and and_1 (and_1_out, START, nor_1_out);
  or or_1 (or_1_out, TICK_6, and_1_out, RESET);
  not not_1 (not_1_out, RESET);
  D_Flip_Flop d_ff_1 (.clk(CLOCK), .D(or_1_out), .Q(TICK_0), .en(1'b1));  // open: Qn, preset, reset
  and and_2 (and_2_out, TICK_0, not_1_out);
  D_Flip_Flop d_ff_2 (.clk(CLOCK), .D(and_2_out), .Q(TICK_1), .en(1'b1));  // open: Qn, preset, reset
  D_Flip_Flop d_ff_3 (.clk(CLOCK), .D(and_3_out), .Q(TICK_2), .en(1'b1));  // open: Qn, preset, reset
  and and_3 (and_3_out, TICK_1, not_1_out);
  and and_4 (and_4_out, TICK_2, not_1_out);
  D_Flip_Flop d_ff_4 (.clk(CLOCK), .D(and_4_out), .Q(TICK_3), .en(1'b1));  // open: Qn, preset, reset
  and and_5 (and_5_out, TICK_3, not_1_out);
  D_Flip_Flop d_ff_5 (.clk(CLOCK), .D(and_5_out), .Q(TICK_4), .en(1'b1));  // open: Qn, preset, reset
  and and_6 (and_6_out, TICK_4, not_1_out);
  D_Flip_Flop d_ff_6 (.clk(CLOCK), .D(and_6_out), .Q(TICK_5), .en(1'b1));  // open: Qn, preset, reset
  and and_7 (and_7_out, TICK_5, not_1_out);
  D_Flip_Flop d_ff_7 (.clk(CLOCK), .D(and_7_out), .Q(TICK_6), .en(1'b1));  // open: Qn, preset, reset
endmodule

// CONTROLLER
module Controller (
  input  [7:0] INSTRUCTION,
  input  CLOCK,
  input  TICK0,
  input  TICK1,
  input  TICK2,
  input  TICK3,
  input  TICK4,
  input  TICK5,
  input  TICK6,
  input  _0,
  output IP_WRITE_ON_AB,
  output INSTR_CACHE_WRITE,
  output RESET,
  output [7:0] CTRL,
  output CACHE0_WRITE,
  output CACHE1_WRITE,
  output IP_WRITE,
  output DA_CACHE_WRITE,
  output DA_CACHE_WRITE_ON_BUS,
  output DD_CACHE_WRITE,
  output DD_CACHE_WRITE_ON_BUS,
  output OPWRITE,
  output OPSELECT0,
  output OPSELECT1,
  output OPSELECT2,
  output OPSELECT3,
  output IP_SOURCE,
  output STATUS_WRITE_ON_BUS,
  output IP_WRITE_ON_DB
);

  Pull_Resistor pull_resistor_1 (.node(TICK5));
  Pull_Resistor pull_resistor_2 (.node(TICK4));
  Pull_Resistor pull_resistor_3 (.node(_0));
  Pull_Resistor pull_resistor_4 (.node(TICK3));
  Pull_Resistor pull_resistor_5 (.node(TICK6));
  Pull_Resistor pull_resistor_6 (.node(TICK0));
  Pull_Resistor pull_resistor_7 (.node(TICK1));
  Pull_Resistor pull_resistor_8 (.node(TICK2));
  Instruction_loader instruction_loader_1 (
    .TICK0(TICK0), .IP_WRITE_ON_BUS(IP_WRITE_ON_AB), .CTRL_WRITE_ON_BUS(CTRL[1]),
    .INSTR_CACHE_WRITE(INSTR_CACHE_WRITE));
  _0x08_8d_ALUCacheLoad u_0x08_8d_alucacheload_1 (
    .INSTR(INSTRUCTION), .TICK1(TICK1), .TICK2(TICK2), .TICK3(TICK3), .CACHE0_WRITE(CACHE0_WRITE),
    .CACHE1_WRITE(CACHE1_WRITE), .IP_WRITE_ON_BUS(IP_WRITE_ON_AB), .IP_WRITE(IP_WRITE),
    .CTRL_WRITE_ON_BUS(CTRL[1]), .DA_CACHE_WRITE(DA_CACHE_WRITE), .RESET(RESET),
    .DA_CACHE_WRITE_ON_BUS(DA_CACHE_WRITE_ON_BUS), .STATUS_WRITE_ON_BUS(STATUS_WRITE_ON_BUS));
  _0x10_9f_ALUOP u_0x10_9f_aluop_1 (
    .INSTR(INSTRUCTION), .TICK1(TICK1), .TICK2(TICK2), .TICK3(TICK3), .OPWRITE(OPWRITE),
    .OPSELECT0(OPSELECT0), .OPSELECT1(OPSELECT1), .OPSELECT2(OPSELECT2), .OPSELECT3(OPSELECT3),
    .CACHE0_WRITE(CACHE0_WRITE), .IP_WRITE_ON_BUS(IP_WRITE_ON_AB), .IP_WRITE(IP_WRITE),
    .CTRL_WRITE_ON_BUS(CTRL[1]), .DA_CACHE_WRITE(DA_CACHE_WRITE), .RESET(RESET),
    .DA_CACHE_WRITE_ON_BUS(DA_CACHE_WRITE_ON_BUS), .DD_CACHE_WRITE(DD_CACHE_WRITE),
    .DD_CACHE_WRITE_ON_BUS(DD_CACHE_WRITE_ON_BUS), .CTRL_WRITE(CTRL[0]));
  _0x20_A0_COPY u_0x20_a0_copy_1 (
    .INSTR(INSTRUCTION), .TICK1(TICK1), .TICK2(TICK2), .TICK3(TICK3), .TICK4(TICK4), .TICK5(TICK5),
    .TICK6(TICK6), .IP_WRITE_ON_BUS(IP_WRITE_ON_AB), .IP_WRITE(IP_WRITE), .CTRL_WRITE_ON_BUS(CTRL[1]),
    .DA_CACHE_WRITE(DA_CACHE_WRITE), .RESET(RESET), .DA_CACHE_WRITE_ON_BUS(DA_CACHE_WRITE_ON_BUS),
    .DD_CACHE_WRITE(DD_CACHE_WRITE), .DD_CACHE_WRITE_ON_BUS(DD_CACHE_WRITE_ON_BUS), .CTRL_WRITE(CTRL[0]));
  _0x30_IP_TO_MEMORY u_0x30_ip_to_memory_1 (
    .INSTR(INSTRUCTION), .TICK1(TICK1), .TICK2(TICK2), .TICK3(TICK3), .IP_WRITE_ON_DB(IP_WRITE_ON_DB),
    .IP_WRITE(IP_WRITE), .DA_CACHE_WRITE(DA_CACHE_WRITE), .DA_CACHE_WRITE_ON_BUS(DA_CACHE_WRITE_ON_BUS),
    .CTRL_WRITE(CTRL[0]), .IP_WRITE_ON_AB(IP_WRITE_ON_AB), .CTRL_WRITE_ON_BUS(CTRL[1]), .RESET(RESET));
  _0x28_a8_Jump u_0x28_a8_jump_1 (
    .INSTR(INSTRUCTION), .TICK1(TICK1), .TICK2(TICK2), .TICK3(TICK3), ._0(_0),
    .IP_WRITE_ON_BUS(IP_WRITE_ON_AB), .IP_WRITE(IP_WRITE), .CTRL_WRITE_ON_BUS(CTRL[1]),
    .DA_CACHE_WRITE(DA_CACHE_WRITE), .RESET(RESET), .DA_CACHE_WRITE_ON_BUS(DA_CACHE_WRITE_ON_BUS),
    .DD_CACHE_WRITE(DD_CACHE_WRITE), .DD_CACHE_WRITE_ON_BUS(DD_CACHE_WRITE_ON_BUS), .IP_SOURCE(IP_SOURCE));
  _0x00_Idle u_0x00_idle_1 (.INSTR(INSTRUCTION), .TICK1(TICK1), .RESET(RESET));
  Pull_Resistor pull_resistor_9 (.node(OPSELECT0));
  Pull_Resistor pull_resistor_10 (.node(OPSELECT2));
  Pull_Resistor pull_resistor_11 (.node(OPSELECT1));
  Pull_Resistor pull_resistor_12 (.node(OPWRITE));
  Pull_Resistor pull_resistor_13 (.node(DA_CACHE_WRITE_ON_BUS));
  Pull_Resistor pull_resistor_14 (.node(DD_CACHE_WRITE_ON_BUS));
  Pull_Resistor pull_resistor_15 (.node(IP_WRITE_ON_AB));
  Pull_Resistor pull_resistor_16 (.node(DA_CACHE_WRITE));
  Pull_Resistor pull_resistor_17 (.node(DD_CACHE_WRITE));
  Pull_Resistor pull_resistor_18 (.node(IP_WRITE));
  Pull_Resistor pull_resistor_19 (.node(CTRL[4]));
  Pull_Resistor pull_resistor_20 (.node(CACHE0_WRITE));
  Pull_Resistor pull_resistor_21 (.node(CTRL[1]));
  Pull_Resistor pull_resistor_22 (.node(CTRL[3]));
  Pull_Resistor pull_resistor_23 (.node(CTRL[0]));
  Pull_Resistor pull_resistor_24 (.node(CACHE1_WRITE));
  Pull_Resistor pull_resistor_25 (.node(RESET));
  Pull_Resistor pull_resistor_26 (.node(CTRL[6]));
  Pull_Resistor pull_resistor_27 (.node(CTRL[5]));
  Pull_Resistor pull_resistor_28 (.node(OPSELECT3));
  Pull_Resistor pull_resistor_29 (.node(CTRL[7]));
  Pull_Resistor pull_resistor_30 (.node(IP_WRITE_ON_DB));
  Pull_Resistor pull_resistor_31 (.node(IP_SOURCE));
  Pull_Resistor pull_resistor_32 (.node(STATUS_WRITE_ON_BUS));

  assign CTRL[2] = CLOCK;

  // Notes on the sheet:
  //   CTRL_READ_FROM_BUS
  //   CTRL_WRITE_ON_BUS
endmodule

// AND
module BITWISE_AND (
  input  [7:0] in_1,
  input  [7:0] in_2,
  output [7:0] out_3
);

  and and_1 (out_3[0], in_1[0], in_2[0]);
  and and_2 (out_3[1], in_1[1], in_2[1]);
  and and_3 (out_3[2], in_1[2], in_2[2]);
  and and_4 (out_3[3], in_1[3], in_2[3]);
  and and_5 (out_3[4], in_1[4], in_2[4]);
  and and_6 (out_3[5], in_1[5], in_2[5]);
  and and_7 (out_3[6], in_1[6], in_2[6]);
  and and_8 (out_3[7], in_1[7], in_2[7]);
endmodule

// OR
module BITWISE_OR (
  input  [7:0] in_1,
  input  [7:0] in_2,
  output [7:0] out_3
);

  or or_1 (out_3[0], in_1[0], in_2[0]);
  or or_2 (out_3[1], in_1[1], in_2[1]);
  or or_3 (out_3[2], in_1[2], in_2[2]);
  or or_4 (out_3[3], in_1[3], in_2[3]);
  or or_5 (out_3[4], in_1[4], in_2[4]);
  or or_6 (out_3[5], in_1[5], in_2[5]);
  or or_7 (out_3[6], in_1[6], in_2[6]);
  or or_8 (out_3[7], in_1[7], in_2[7]);
endmodule

// XOR
module BITWISE_XOR (
  input  [7:0] in_1,
  input  [7:0] in_2,
  output [7:0] out_3
);

  xor xor_1 (out_3[0], in_1[0], in_2[0]);
  xor xor_2 (out_3[1], in_1[1], in_2[1]);
  xor xor_3 (out_3[2], in_1[2], in_2[2]);
  xor xor_4 (out_3[3], in_1[3], in_2[3]);
  xor xor_5 (out_3[4], in_1[4], in_2[4]);
  xor xor_6 (out_3[5], in_1[5], in_2[5]);
  xor xor_7 (out_3[6], in_1[6], in_2[6]);
  xor xor_8 (out_3[7], in_1[7], in_2[7]);
endmodule

// INV
module _8BIT_INVERTER (
  input  [7:0] in_1,
  output [7:0] out_2
);

  not not_1 (out_2[0], in_1[0]);
  not not_2 (out_2[1], in_1[1]);
  not not_3 (out_2[2], in_1[2]);
  not not_4 (out_2[3], in_1[3]);
  not not_5 (out_2[4], in_1[4]);
  not not_6 (out_2[5], in_1[5]);
  not not_7 (out_2[6], in_1[6]);
  not not_8 (out_2[7], in_1[7]);
endmodule

// CacheLoad
module _0x08_8d_ALUCacheLoad (
  input  [7:0] INSTR,
  input  TICK1,
  input  TICK2,
  input  TICK3,
  output CACHE0_WRITE,
  output CACHE1_WRITE,
  output IP_WRITE_ON_BUS,
  output IP_WRITE,
  output CTRL_WRITE_ON_BUS,
  output DA_CACHE_WRITE,
  output RESET,
  output DA_CACHE_WRITE_ON_BUS,
  output STATUS_WRITE_ON_BUS
);

  wire and_1_out, and_2_out, and_3_out, and_4_out, and_5_out, and_6_out, and_7_out, comparator_1_eq,
       or_1_out, or_2_out, or_3_out;

  or or_1 (or_1_out, TICK3, TICK2, TICK1);
  Comparator comparator_1 (.a(8'h8), .b({1'b0, INSTR[6:3], 3'b000}), .eq(comparator_1_eq));  // open: gt, lt
  and and_1 (and_1_out, comparator_1_eq, or_1_out);
  and and_2 (and_2_out, INSTR[7], TICK2);
  and and_3 (and_3_out, TICK2, ~INSTR[7]);  // AND_Gate
  and and_4 (and_4_out, ~INSTR[2], TICK1);  // AND_Gate
  and and_5 (and_5_out, INSTR[2], TICK1);
  or or_2 (or_2_out, and_2_out, and_5_out, TICK3);
  and and_6 (and_6_out, INSTR[0], or_2_out);
  and and_7 (and_7_out, ~INSTR[0], or_2_out);  // AND_Gate
  or or_3 (or_3_out, TICK2, TICK3);
  assign CACHE0_WRITE = and_1_out ? and_7_out : 1'bz;  // Controlled_Buffer controlled_buffer_1
  assign CACHE1_WRITE = and_1_out ? and_6_out : 1'bz;  // Controlled_Buffer controlled_buffer_2
  assign IP_WRITE_ON_BUS = and_1_out ? TICK2 : 1'bz;  // Controlled_Buffer controlled_buffer_3
  assign IP_WRITE = and_1_out ? and_4_out : 1'bz;  // Controlled_Buffer controlled_buffer_4
  assign CTRL_WRITE_ON_BUS = and_1_out ? or_3_out : 1'bz;  // Controlled_Buffer controlled_buffer_5
  assign DA_CACHE_WRITE = and_1_out ? and_3_out : 1'bz;  // Controlled_Buffer controlled_buffer_6
  assign RESET = and_1_out ? or_2_out : 1'bz;  // Controlled_Buffer controlled_buffer_7
  assign DA_CACHE_WRITE_ON_BUS = and_1_out ? TICK3 : 1'bz;  // Controlled_Buffer controlled_buffer_8
  assign STATUS_WRITE_ON_BUS = and_1_out ? and_5_out : 1'bz;  // Controlled_Buffer controlled_buffer_9

  // Notes on the sheet:
  //   IMMEDIATE
  //   FROM_STATUS
endmodule

// IL
module Instruction_loader (
  input  TICK0,
  output IP_WRITE_ON_BUS,
  output CTRL_WRITE_ON_BUS,
  output INSTR_CACHE_WRITE
);

  assign IP_WRITE_ON_BUS = TICK0 ? TICK0 : 1'bz;  // Controlled_Buffer controlled_buffer_1
  assign CTRL_WRITE_ON_BUS = TICK0 ? TICK0 : 1'bz;  // Controlled_Buffer controlled_buffer_2

  assign INSTR_CACHE_WRITE = TICK0;
endmodule

module BUFFER_DELAY (
  input  IN,
  output OUT
);

  wire buffer_1_out, buffer_2_out, buffer_3_out, buffer_4_out, buffer_5_out, buffer_6_out, buffer_7_out,
       buffer_8_out, buffer_9_out, buffer_10_out, buffer_11_out, buffer_12_out, buffer_13_out, buffer_14_out,
       buffer_15_out, buffer_16_out, buffer_17_out, buffer_18_out, buffer_19_out, buffer_20_out,
       buffer_21_out, buffer_22_out, buffer_23_out, buffer_24_out, buffer_25_out, buffer_26_out,
       buffer_27_out, buffer_28_out, buffer_29_out, buffer_30_out, buffer_31_out, buffer_32_out,
       buffer_33_out, buffer_34_out, buffer_35_out, buffer_36_out, buffer_37_out, buffer_38_out,
       buffer_39_out, buffer_40_out, buffer_41_out, buffer_42_out, buffer_43_out, buffer_44_out,
       buffer_45_out, buffer_46_out, buffer_47_out, buffer_48_out, buffer_49_out, buffer_50_out,
       buffer_51_out, buffer_52_out, buffer_53_out, buffer_54_out, buffer_55_out, buffer_56_out,
       buffer_57_out, buffer_58_out, buffer_59_out, buffer_60_out, buffer_61_out, buffer_62_out,
       buffer_63_out, buffer_64_out, buffer_65_out, buffer_66_out, buffer_67_out, buffer_68_out,
       buffer_69_out, buffer_70_out, buffer_71_out, buffer_72_out, buffer_73_out, buffer_74_out,
       buffer_75_out, buffer_76_out, buffer_77_out, buffer_78_out, buffer_79_out, buffer_80_out,
       buffer_81_out, buffer_82_out, buffer_83_out, buffer_84_out, buffer_85_out, buffer_86_out,
       buffer_87_out, buffer_88_out, buffer_89_out, buffer_90_out, buffer_91_out, buffer_92_out,
       buffer_93_out, buffer_94_out, buffer_95_out, buffer_96_out, buffer_97_out, buffer_98_out,
       buffer_99_out, buffer_100_out, buffer_101_out, buffer_102_out, buffer_103_out, buffer_104_out,
       buffer_105_out, buffer_106_out, buffer_107_out, buffer_108_out, buffer_109_out, buffer_110_out,
       buffer_111_out, buffer_112_out, buffer_113_out, buffer_114_out, buffer_115_out, buffer_116_out,
       buffer_117_out, buffer_118_out, buffer_120_out;

  buf buffer_1 (buffer_1_out, buffer_2_out);
  buf buffer_2 (buffer_2_out, buffer_4_out);
  buf buffer_3 (buffer_3_out, IN);
  buf buffer_4 (buffer_4_out, buffer_6_out);
  buf buffer_5 (buffer_5_out, buffer_3_out);
  buf buffer_6 (buffer_6_out, buffer_9_out);
  buf buffer_7 (buffer_7_out, buffer_5_out);
  buf buffer_8 (buffer_8_out, buffer_7_out);
  buf buffer_9 (buffer_9_out, buffer_10_out);
  buf buffer_10 (buffer_10_out, buffer_13_out);
  buf buffer_11 (buffer_11_out, buffer_8_out);
  buf buffer_12 (buffer_12_out, buffer_11_out);
  buf buffer_13 (buffer_13_out, buffer_14_out);
  buf buffer_14 (buffer_14_out, buffer_17_out);
  buf buffer_15 (buffer_15_out, buffer_12_out);
  buf buffer_16 (buffer_16_out, buffer_15_out);
  buf buffer_17 (buffer_17_out, buffer_18_out);
  buf buffer_18 (buffer_18_out, buffer_20_out);
  buf buffer_19 (buffer_19_out, buffer_16_out);
  buf buffer_20 (buffer_20_out, buffer_22_out);
  buf buffer_21 (buffer_21_out, buffer_19_out);
  buf buffer_22 (buffer_22_out, buffer_24_out);
  buf buffer_23 (buffer_23_out, buffer_21_out);
  buf buffer_24 (buffer_24_out, buffer_26_out);
  buf buffer_25 (buffer_25_out, buffer_23_out);
  buf buffer_26 (buffer_26_out, buffer_28_out);
  buf buffer_27 (buffer_27_out, buffer_25_out);
  buf buffer_28 (buffer_28_out, buffer_30_out);
  buf buffer_29 (buffer_29_out, buffer_27_out);
  buf buffer_30 (buffer_30_out, buffer_33_out);
  buf buffer_31 (buffer_31_out, buffer_29_out);
  buf buffer_32 (buffer_32_out, buffer_31_out);
  buf buffer_33 (buffer_33_out, buffer_35_out);
  buf buffer_34 (buffer_34_out, buffer_32_out);
  buf buffer_35 (buffer_35_out, buffer_37_out);
  buf buffer_36 (buffer_36_out, buffer_34_out);
  buf buffer_37 (buffer_37_out, buffer_38_out);
  buf buffer_38 (buffer_38_out, buffer_40_out);
  buf buffer_39 (buffer_39_out, buffer_36_out);
  buf buffer_40 (buffer_40_out, buffer_42_out);
  buf buffer_41 (buffer_41_out, buffer_39_out);
  buf buffer_42 (buffer_42_out, buffer_45_out);
  buf buffer_43 (buffer_43_out, buffer_41_out);
  buf buffer_44 (buffer_44_out, buffer_43_out);
  buf buffer_45 (buffer_45_out, buffer_46_out);
  buf buffer_46 (buffer_46_out, buffer_48_out);
  buf buffer_47 (buffer_47_out, buffer_44_out);
  buf buffer_48 (buffer_48_out, buffer_47_out);
  buf buffer_49 (buffer_49_out, buffer_50_out);
  buf buffer_50 (buffer_50_out, buffer_54_out);
  buf buffer_51 (buffer_51_out, buffer_49_out);
  buf buffer_52 (buffer_52_out, buffer_1_out);
  buf buffer_53 (buffer_53_out, buffer_51_out);
  buf buffer_54 (buffer_54_out, buffer_58_out);
  buf buffer_55 (buffer_55_out, buffer_52_out);
  buf buffer_56 (buffer_56_out, buffer_55_out);
  buf buffer_57 (buffer_57_out, buffer_53_out);
  buf buffer_58 (buffer_58_out, buffer_60_out);
  buf buffer_59 (buffer_59_out, buffer_57_out);
  buf buffer_60 (buffer_60_out, buffer_64_out);
  buf buffer_61 (buffer_61_out, buffer_56_out);
  buf buffer_62 (buffer_62_out, buffer_61_out);
  buf buffer_63 (buffer_63_out, buffer_59_out);
  buf buffer_64 (buffer_64_out, buffer_65_out);
  buf buffer_65 (buffer_65_out, buffer_68_out);
  buf buffer_66 (buffer_66_out, buffer_63_out);
  buf buffer_67 (buffer_67_out, buffer_62_out);
  buf buffer_68 (buffer_68_out, buffer_71_out);
  buf buffer_69 (buffer_69_out, buffer_66_out);
  buf buffer_70 (buffer_70_out, buffer_67_out);
  buf buffer_71 (buffer_71_out, buffer_76_out);
  buf buffer_72 (buffer_72_out, buffer_69_out);
  buf buffer_73 (buffer_73_out, buffer_70_out);
  buf buffer_74 (buffer_74_out, buffer_73_out);
  buf buffer_75 (buffer_75_out, buffer_72_out);
  buf buffer_76 (buffer_76_out, buffer_79_out);
  buf buffer_77 (buffer_77_out, buffer_74_out);
  buf buffer_78 (buffer_78_out, buffer_75_out);
  buf buffer_79 (buffer_79_out, buffer_81_out);
  buf buffer_80 (buffer_80_out, buffer_78_out);
  buf buffer_81 (buffer_81_out, buffer_85_out);
  buf buffer_82 (buffer_82_out, buffer_77_out);
  buf buffer_83 (buffer_83_out, buffer_82_out);
  buf buffer_84 (buffer_84_out, buffer_80_out);
  buf buffer_85 (buffer_85_out, buffer_88_out);
  buf buffer_86 (buffer_86_out, buffer_83_out);
  buf buffer_87 (buffer_87_out, buffer_84_out);
  buf buffer_88 (buffer_88_out, buffer_91_out);
  buf buffer_89 (buffer_89_out, buffer_87_out);
  buf buffer_90 (buffer_90_out, buffer_86_out);
  buf buffer_91 (buffer_91_out, buffer_93_out);
  buf buffer_92 (buffer_92_out, buffer_90_out);
  buf buffer_93 (buffer_93_out, buffer_97_out);
  buf buffer_94 (buffer_94_out, buffer_89_out);
  buf buffer_95 (buffer_95_out, buffer_92_out);
  buf buffer_96 (buffer_96_out, buffer_94_out);
  buf buffer_97 (buffer_97_out, buffer_100_out);
  buf buffer_98 (buffer_98_out, buffer_96_out);
  buf buffer_99 (buffer_99_out, buffer_95_out);
  buf buffer_100 (buffer_100_out, buffer_102_out);
  buf buffer_101 (buffer_101_out, buffer_98_out);
  buf buffer_102 (buffer_102_out, buffer_104_out);
  buf buffer_103 (buffer_103_out, buffer_99_out);
  buf buffer_104 (buffer_104_out, buffer_109_out);
  buf buffer_105 (buffer_105_out, buffer_101_out);
  buf buffer_106 (buffer_106_out, buffer_103_out);
  buf buffer_107 (buffer_107_out, buffer_106_out);
  buf buffer_108 (buffer_108_out, buffer_105_out);
  buf buffer_109 (buffer_109_out, buffer_110_out);
  buf buffer_110 (buffer_110_out, buffer_114_out);
  buf buffer_111 (buffer_111_out, buffer_108_out);
  buf buffer_112 (buffer_112_out, buffer_107_out);
  buf buffer_113 (buffer_113_out, buffer_112_out);
  buf buffer_114 (buffer_114_out, buffer_116_out);
  buf buffer_115 (buffer_115_out, buffer_111_out);
  buf buffer_116 (buffer_116_out, buffer_120_out);
  buf buffer_117 (buffer_117_out, buffer_113_out);
  buf buffer_118 (buffer_118_out, buffer_115_out);
  buf buffer_119 (OUT, buffer_118_out);
  buf buffer_120 (buffer_120_out, buffer_117_out);
endmodule

// ALUOP
module _0x10_9f_ALUOP (
  input  [7:0] INSTR,
  input  TICK1,
  input  TICK2,
  input  TICK3,
  output OPWRITE,
  output OPSELECT0,
  output OPSELECT1,
  output OPSELECT2,
  output OPSELECT3,
  output CACHE0_WRITE,
  output IP_WRITE_ON_BUS,
  output IP_WRITE,
  output CTRL_WRITE_ON_BUS,
  output DA_CACHE_WRITE,
  output RESET,
  output DA_CACHE_WRITE_ON_BUS,
  output DD_CACHE_WRITE,
  output DD_CACHE_WRITE_ON_BUS,
  output CTRL_WRITE
);

  wire and_1_out, and_2_out, and_3_out, and_4_out, and_5_out, and_6_out, comparator_1_eq, or_1_out, or_2_out,
       or_3_out;

  or or_1 (or_1_out, TICK3, TICK2, TICK1);
  Comparator comparator_1 (.a(8'h10), .b({1'b0, INSTR[6:4], 4'b0000}), .eq(comparator_1_eq));  // open: gt, lt
  and and_1 (and_1_out, comparator_1_eq, or_1_out);
  and and_2 (and_2_out, INSTR[7], TICK1);
  and and_3 (and_3_out, INSTR[7], TICK2);
  and and_4 (and_4_out, ~INSTR[7], TICK1);  // AND_Gate
  and and_5 (and_5_out, ~INSTR[7], TICK2);  // AND_Gate
  and and_6 (and_6_out, ~INSTR[7], TICK3);  // AND_Gate
  or or_2 (or_2_out, and_6_out, and_2_out);
  or or_3 (or_3_out, and_3_out, and_6_out);
  assign OPWRITE = and_1_out ? or_2_out : 1'bz;  // Controlled_Buffer controlled_buffer_1
  assign OPSELECT0 = and_1_out ? INSTR[0] : 1'bz;  // Controlled_Buffer controlled_buffer_2
  assign OPSELECT1 = and_1_out ? INSTR[1] : 1'bz;  // Controlled_Buffer controlled_buffer_3
  assign OPSELECT2 = and_1_out ? INSTR[2] : 1'bz;  // Controlled_Buffer controlled_buffer_4
  assign OPSELECT3 = and_1_out ? INSTR[3] : 1'bz;  // Controlled_Buffer controlled_buffer_5
  assign CACHE0_WRITE = and_1_out ? and_3_out : 1'bz;  // Controlled_Buffer controlled_buffer_6
  assign IP_WRITE_ON_BUS = and_1_out ? and_5_out : 1'bz;  // Controlled_Buffer controlled_buffer_7
  assign IP_WRITE = and_1_out ? and_4_out : 1'bz;  // Controlled_Buffer controlled_buffer_8
  assign CTRL_WRITE_ON_BUS = and_1_out ? and_5_out : 1'bz;  // Controlled_Buffer controlled_buffer_9
  assign DA_CACHE_WRITE = and_1_out ? and_5_out : 1'bz;  // Controlled_Buffer controlled_buffer_10
  assign RESET = and_1_out ? or_3_out : 1'bz;  // Controlled_Buffer controlled_buffer_11
  assign DA_CACHE_WRITE_ON_BUS = and_1_out ? and_6_out : 1'bz;  // Controlled_Buffer controlled_buffer_12
  assign DD_CACHE_WRITE = and_1_out ? and_2_out : 1'bz;  // Controlled_Buffer controlled_buffer_13
  assign DD_CACHE_WRITE_ON_BUS = and_1_out ? and_3_out : 1'bz;  // Controlled_Buffer controlled_buffer_14
  assign CTRL_WRITE = and_1_out ? and_6_out : 1'bz;  // Controlled_Buffer controlled_buffer_15

  // Notes on the sheet:
  //   TO CACHE
endmodule

// COPY
module _0x20_A0_COPY (
  input  [7:0] INSTR,
  input  TICK1,
  input  TICK2,
  input  TICK3,
  input  TICK4,
  input  TICK5,
  input  TICK6,
  output IP_WRITE_ON_BUS,
  output IP_WRITE,
  output CTRL_WRITE_ON_BUS,
  output DA_CACHE_WRITE,
  output RESET,
  output DA_CACHE_WRITE_ON_BUS,
  output DD_CACHE_WRITE,
  output DD_CACHE_WRITE_ON_BUS,
  output CTRL_WRITE
);

  wire and_1_out, and_2_out, and_3_out, and_4_out, and_5_out, and_6_out, and_7_out, and_8_out, and_9_out,
       and_10_out, and_11_out, and_12_out, comparator_1_eq, or_1_out, or_2_out, or_3_out, or_4_out, or_5_out,
       or_6_out, or_7_out, or_8_out, or_9_out, or_10_out;

  or or_1 (or_1_out, TICK1, TICK2, TICK3, TICK4, TICK5, TICK6);
  Comparator comparator_1 (.a(8'h20), .b({1'b0, INSTR[6:3], 3'b000}), .eq(comparator_1_eq));  // open: gt, lt
  and and_1 (and_1_out, comparator_1_eq, or_1_out);
  and and_2 (and_2_out, INSTR[7], TICK1);
  and and_3 (and_3_out, INSTR[7], TICK2);
  and and_4 (and_4_out, INSTR[7], TICK3);
  and and_5 (and_5_out, INSTR[7], TICK4);
  and and_6 (and_6_out, INSTR[7], TICK5);
  and and_7 (and_7_out, ~INSTR[7], TICK1);  // AND_Gate
  and and_8 (and_8_out, ~INSTR[7], TICK2);  // AND_Gate
  and and_9 (and_9_out, ~INSTR[7], TICK3);  // AND_Gate
  and and_10 (and_10_out, ~INSTR[7], TICK4);  // AND_Gate
  and and_11 (and_11_out, ~INSTR[7], TICK5);  // AND_Gate
  and and_12 (and_12_out, ~INSTR[7], TICK6);  // AND_Gate
  or or_2 (or_2_out, and_4_out, and_2_out, and_7_out, and_10_out);
  or or_3 (or_3_out, and_3_out, and_5_out, and_8_out, and_11_out);
  or or_4 (or_4_out, and_8_out, and_3_out, and_11_out, and_5_out, and_9_out);
  or or_5 (or_5_out, and_8_out, and_5_out, and_11_out);
  or or_6 (or_6_out, and_12_out, and_6_out);
  or or_7 (or_7_out, and_9_out, and_6_out, and_12_out);
  or or_8 (or_8_out, and_3_out, and_9_out);
  or or_9 (or_9_out, and_6_out, and_12_out);
  or or_10 (or_10_out, and_6_out, and_12_out);
  assign IP_WRITE_ON_BUS = and_1_out ? or_3_out : 1'bz;  // Controlled_Buffer controlled_buffer_1
  assign IP_WRITE = and_1_out ? or_2_out : 1'bz;  // Controlled_Buffer controlled_buffer_2
  assign CTRL_WRITE_ON_BUS = and_1_out ? or_4_out : 1'bz;  // Controlled_Buffer controlled_buffer_3
  assign DA_CACHE_WRITE = and_1_out ? or_5_out : 1'bz;  // Controlled_Buffer controlled_buffer_4
  assign RESET = and_1_out ? or_6_out : 1'bz;  // Controlled_Buffer controlled_buffer_5
  assign DA_CACHE_WRITE_ON_BUS = and_1_out ? or_7_out : 1'bz;  // Controlled_Buffer controlled_buffer_6
  assign DD_CACHE_WRITE = and_1_out ? or_8_out : 1'bz;  // Controlled_Buffer controlled_buffer_7
  assign DD_CACHE_WRITE_ON_BUS = and_1_out ? or_9_out : 1'bz;  // Controlled_Buffer controlled_buffer_8
  assign CTRL_WRITE = and_1_out ? or_10_out : 1'bz;  // Controlled_Buffer controlled_buffer_9

  // Notes on the sheet:
  //   IMMEDIATE
endmodule

// JUMP
module _0x28_a8_Jump (
  input  [7:0] INSTR,
  input  TICK1,
  input  TICK2,
  input  TICK3,
  input  _0,
  output IP_WRITE_ON_BUS,
  output IP_WRITE,
  output CTRL_WRITE_ON_BUS,
  output DA_CACHE_WRITE,
  output RESET,
  output DA_CACHE_WRITE_ON_BUS,
  output DD_CACHE_WRITE,
  output DD_CACHE_WRITE_ON_BUS,
  output IP_SOURCE
);

  wire and_1_out, and_2_out, and_3_out, and_4_out, and_5_out, and_6_out, and_7_out, comparator_1_eq,
       or_1_out, or_2_out, or_3_out, or_4_out;

  or or_1 (or_1_out, TICK1, TICK2, TICK3);
  Comparator comparator_1 (.a(8'h28), .b({1'b0, INSTR[6:3], 3'b000}), .eq(comparator_1_eq));  // open: gt, lt
  and and_1 (and_1_out, comparator_1_eq, or_1_out);
  and and_2 (and_2_out, TICK2, INSTR[7]);
  and and_3 (and_3_out, TICK2, ~INSTR[7]);  // AND_Gate
  and and_4 (and_4_out, TICK3, INSTR[7]);
  and and_5 (and_5_out, TICK3, ~INSTR[7]);  // AND_Gate
  and and_6 (and_6_out, TICK1, ~_0);  // AND_Gate
  and and_7 (and_7_out, TICK1, _0);
  or or_2 (or_2_out, and_7_out, TICK3);
  or or_3 (or_3_out, TICK2, and_5_out);
  or or_4 (or_4_out, TICK3, and_6_out);
  assign IP_WRITE_ON_BUS = and_1_out ? TICK2 : 1'bz;  // Controlled_Buffer controlled_buffer_1
  assign IP_WRITE = and_1_out ? or_2_out : 1'bz;  // Controlled_Buffer controlled_buffer_2
  assign CTRL_WRITE_ON_BUS = and_1_out ? or_3_out : 1'bz;  // Controlled_Buffer controlled_buffer_3
  assign DA_CACHE_WRITE = and_1_out ? and_3_out : 1'bz;  // Controlled_Buffer controlled_buffer_4
  assign RESET = and_1_out ? or_4_out : 1'bz;  // Controlled_Buffer controlled_buffer_5
  assign DA_CACHE_WRITE_ON_BUS = and_1_out ? and_5_out : 1'bz;  // Controlled_Buffer controlled_buffer_6
  assign DD_CACHE_WRITE = and_1_out ? and_2_out : 1'bz;  // Controlled_Buffer controlled_buffer_7
  assign DD_CACHE_WRITE_ON_BUS = and_1_out ? and_4_out : 1'bz;  // Controlled_Buffer controlled_buffer_8
  assign IP_SOURCE = and_1_out ? TICK3 : 1'bz;  // Controlled_Buffer controlled_buffer_9

  // Notes on the sheet:
  //   IMMEDIATE
endmodule

module _0x00_Idle (
  input  [7:0] INSTR,
  input  TICK1,
  output RESET
);

  wire and_1_out, comparator_1_eq;

  Comparator comparator_1 (.a({8{1'b0}}), .b({1'b0, INSTR[6:3], 3'b000}), .eq(comparator_1_eq));  // open: gt, lt
  and and_1 (and_1_out, comparator_1_eq, TICK1);
  assign RESET = and_1_out ? and_1_out : 1'bz;  // Controlled_Buffer controlled_buffer_1
endmodule

module DISPLAYCTRL (
  input  [7:0] CTRL,
  input  [7:0] DATA,
  input  [7:0] ADDRESS,
  output CLOCK,
  output [6:0] DATA_2,
  output SELECT
);

  Bit_Extender #(.out_width(7)) bit_extender_1 (.in(DATA), .out(DATA_2));
  Comparator comparator_1 (.a(ADDRESS), .b(8'h80), .eq(SELECT));  // open: gt, lt

  assign CLOCK = CTRL[2];
endmodule

// IP_TO_MEM
module _0x30_IP_TO_MEMORY (
  input  [7:0] INSTR,
  input  TICK1,
  input  TICK2,
  input  TICK3,
  output IP_WRITE_ON_DB,
  output IP_WRITE,
  output DA_CACHE_WRITE,
  output DA_CACHE_WRITE_ON_BUS,
  output CTRL_WRITE,
  output IP_WRITE_ON_AB,
  output CTRL_WRITE_ON_BUS,
  output RESET
);

  wire and_1_out, comparator_1_eq, or_1_out;

  or or_1 (or_1_out, TICK3, TICK2, TICK1);
  Comparator comparator_1 (.a(8'h30), .b({1'b0, INSTR[6:3], 3'b000}), .eq(comparator_1_eq));  // open: gt, lt
  and and_1 (and_1_out, comparator_1_eq, or_1_out);
  assign IP_WRITE_ON_DB = and_1_out ? TICK3 : 1'bz;  // Controlled_Buffer controlled_buffer_1
  assign IP_WRITE = and_1_out ? TICK1 : 1'bz;  // Controlled_Buffer controlled_buffer_2
  assign DA_CACHE_WRITE = and_1_out ? TICK2 : 1'bz;  // Controlled_Buffer controlled_buffer_3
  assign DA_CACHE_WRITE_ON_BUS = and_1_out ? TICK3 : 1'bz;  // Controlled_Buffer controlled_buffer_4
  assign CTRL_WRITE = and_1_out ? TICK3 : 1'bz;  // Controlled_Buffer controlled_buffer_5
  assign IP_WRITE_ON_AB = and_1_out ? TICK2 : 1'bz;  // Controlled_Buffer controlled_buffer_6
  assign CTRL_WRITE_ON_BUS = and_1_out ? TICK2 : 1'bz;  // Controlled_Buffer controlled_buffer_7
  assign RESET = and_1_out ? TICK3 : 1'bz;  // Controlled_Buffer controlled_buffer_8
endmodule
